// Digital circuit circuit.dig as structural Verilog
module circuit (
  input  b_0,
  input  a_0,
  input  b_1,
  input  a_1,
  input  b_2,
  input  a_2,
  input  b_3,
  input  a_3,
  input  op_1,
  input  op_2,
  input  op_3,
  input  op_0,
  output r_0,
  output r_1,
  output r_2,
  output r_3,
  output c_out
);

  wire [0:0] ALU_1_d, ALU_2_d, ALU_3_d;

  ROM #(.AddrBits(6), .Bits(2)) ALU_1 (.A({op_0, op_1, op_2, op_3, a_0, b_0}), .sel(1'b1), .D({r_0, ALU_1_d[0]}));
  ROM #(.AddrBits(7), .Bits(2)) ALU_2 (
    .A({ALU_1_d[0], op_0, op_1, op_2, op_3, a_1, b_1}), .sel(1'b1), .D({r_1, ALU_2_d[0]}));
  ROM #(.AddrBits(7), .Bits(2)) ALU_3 (
    .A({ALU_2_d[0], op_0, op_1, op_2, op_3, a_2, b_2}), .sel(1'b1), .D({r_2, ALU_3_d[0]}));
  ROM #(.AddrBits(7), .Bits(2)) ALU_4 (
    .A({ALU_3_d[0], op_0, op_1, op_2, op_3, a_3, b_3}), .sel(1'b1), .D({r_3, c_out}));

  // Notes on the sheet:
  //   contents of ALU_1 (hex, n*v repeats v):
  //   0,2,2,1,0,0,1,1,0,0,0,2,5*0,2,2,2,5*0,2,2,5*0,2,0,0,2,4*0,2,2,2
  //   ,5*0,2,7*0,2,2
  //   contents of ALU_2 (hex, n*v repeats v):
  //   0,2,2,1,0,0,1,1,0,0,0,2,5*0,2,2,2,5*0,2,2,5*0,2,0,0,2,4*0,2,2,2
  //   ,5*0,2,7*0,2,2,6*0,2,1,1,3,2,2,3,3,0,0,0,2,5*0,2,2,2,5*0,2,2,5*0
  //   ,2,0,0,2,4*0,2,2,2,5*0,2,7*0,2,2
  //   contents of ALU_3 (hex, n*v repeats v):
  //   0,2,2,1,0,0,1,1,0,0,0,2,5*0,2,2,2,5*0,2,2,5*0,2,0,0,2,4*0,2,2,2
  //   ,5*0,2,7*0,2,2,6*0,2,1,1,3,2,2,3,3,0,0,0,2,5*0,2,2,2,5*0,2,2,5*0
  //   ,2,0,0,2,4*0,2,2,2,5*0,2,7*0,2,2
  //   contents of ALU_4 (hex, n*v repeats v):
  //   0,2,2,1,0,0,1,1,0,0,0,2,5*0,2,2,2,5*0,2,2,5*0,2,0,0,2,4*0,2,2,2
  //   ,5*0,2,7*0,2,2,6*0,2,1,1,3,2,2,3,3,0,0,0,2,5*0,2,2,2,5*0,2,2,5*0
  //   ,2,0,0,2,4*0,2,2,2,5*0,2,7*0,2,2
endmodule

/* Test case Somma:
op_0 op_1 op_2 op_3 a_3 a_2 a_1 a_0 b_3 b_2 b_1 b_0 r_3 r_2 r_1 r_0 c_out
0 0 0 0 0 0 0 0 0 0 0 0 0 0 0 0 0
0 0 0 0 0 0 0 0 0 0 0 1 0 0 0 1 0
0 0 0 0 0 0 0 0 0 0 1 0 0 0 1 0 0
0 0 0 0 0 0 0 0 0 0 1 1 0 0 1 1 0
0 0 0 0 0 0 0 0 0 1 0 0 0 1 0 0 0
0 0 0 0 0 0 0 0 0 1 0 1 0 1 0 1 0
0 0 0 0 0 0 0 0 0 1 1 0 0 1 1 0 0
0 0 0 0 0 0 0 0 0 1 1 1 0 1 1 1 0
0 0 0 0 0 0 0 0 1 0 0 0 1 0 0 0 0
0 0 0 0 0 0 0 0 1 0 0 1 1 0 0 1 0
0 0 0 0 0 0 0 0 1 0 1 0 1 0 1 0 0
0 0 0 0 0 0 0 0 1 0 1 1 1 0 1 1 0
0 0 0 0 0 0 0 0 1 1 0 0 1 1 0 0 0
0 0 0 0 0 0 0 0 1 1 0 1 1 1 0 1 0
0 0 0 0 0 0 0 0 1 1 1 0 1 1 1 0 0
0 0 0 0 0 0 0 0 1 1 1 1 1 1 1 1 0
0 0 0 0 0 0 0 1 0 0 0 0 0 0 0 1 0
0 0 0 0 0 0 0 1 0 0 0 1 0 0 1 0 0
0 0 0 0 0 0 0 1 0 0 1 0 0 0 1 1 0
0 0 0 0 0 0 0 1 0 0 1 1 0 1 0 0 0
0 0 0 0 0 0 0 1 0 1 0 0 0 1 0 1 0
0 0 0 0 0 0 0 1 0 1 0 1 0 1 1 0 0
0 0 0 0 0 0 0 1 0 1 1 0 0 1 1 1 0
0 0 0 0 0 0 0 1 0 1 1 1 1 0 0 0 0
0 0 0 0 0 0 0 1 1 0 0 0 1 0 0 1 0
0 0 0 0 0 0 0 1 1 0 0 1 1 0 1 0 0
0 0 0 0 0 0 0 1 1 0 1 0 1 0 1 1 0
0 0 0 0 0 0 0 1 1 0 1 1 1 1 0 0 0
0 0 0 0 0 0 0 1 1 1 0 0 1 1 0 1 0
0 0 0 0 0 0 0 1 1 1 0 1 1 1 1 0 0
0 0 0 0 0 0 0 1 1 1 1 0 1 1 1 1 0
0 0 0 0 0 0 0 1 1 1 1 1 0 0 0 0 1
0 0 0 0 0 0 1 0 0 0 0 0 0 0 1 0 0
0 0 0 0 0 0 1 0 0 0 0 1 0 0 1 1 0
0 0 0 0 0 0 1 0 0 0 1 0 0 1 0 0 0
0 0 0 0 0 0 1 0 0 0 1 1 0 1 0 1 0
0 0 0 0 0 0 1 0 0 1 0 0 0 1 1 0 0
0 0 0 0 0 0 1 0 0 1 0 1 0 1 1 1 0
0 0 0 0 0 0 1 0 0 1 1 0 1 0 0 0 0
0 0 0 0 0 0 1 0 0 1 1 1 1 0 0 1 0
0 0 0 0 0 0 1 0 1 0 0 0 1 0 1 0 0
0 0 0 0 0 0 1 0 1 0 0 1 1 0 1 1 0
0 0 0 0 0 0 1 0 1 0 1 0 1 1 0 0 0
0 0 0 0 0 0 1 0 1 0 1 1 1 1 0 1 0
0 0 0 0 0 0 1 0 1 1 0 0 1 1 1 0 0
0 0 0 0 0 0 1 0 1 1 0 1 1 1 1 1 0
0 0 0 0 0 0 1 0 1 1 1 0 0 0 0 0 1
0 0 0 0 0 0 1 0 1 1 1 1 0 0 0 1 1
0 0 0 0 0 0 1 1 0 0 0 0 0 0 1 1 0
0 0 0 0 0 0 1 1 0 0 0 1 0 1 0 0 0
0 0 0 0 0 0 1 1 0 0 1 0 0 1 0 1 0
0 0 0 0 0 0 1 1 0 0 1 1 0 1 1 0 0
0 0 0 0 0 0 1 1 0 1 0 0 0 1 1 1 0
0 0 0 0 0 0 1 1 0 1 0 1 1 0 0 0 0
0 0 0 0 0 0 1 1 0 1 1 0 1 0 0 1 0
0 0 0 0 0 0 1 1 0 1 1 1 1 0 1 0 0
0 0 0 0 0 0 1 1 1 0 0 0 1 0 1 1 0
0 0 0 0 0 0 1 1 1 0 0 1 1 1 0 0 0
0 0 0 0 0 0 1 1 1 0 1 0 1 1 0 1 0
0 0 0 0 0 0 1 1 1 0 1 1 1 1 1 0 0
0 0 0 0 0 0 1 1 1 1 0 0 1 1 1 1 0
0 0 0 0 0 0 1 1 1 1 0 1 0 0 0 0 1
0 0 0 0 0 0 1 1 1 1 1 0 0 0 0 1 1
0 0 0 0 0 0 1 1 1 1 1 1 0 0 1 0 1
0 0 0 0 0 1 0 0 0 0 0 0 0 1 0 0 0
0 0 0 0 0 1 0 0 0 0 0 1 0 1 0 1 0
0 0 0 0 0 1 0 0 0 0 1 0 0 1 1 0 0
0 0 0 0 0 1 0 0 0 0 1 1 0 1 1 1 0
0 0 0 0 0 1 0 0 0 1 0 0 1 0 0 0 0
0 0 0 0 0 1 0 0 0 1 0 1 1 0 0 1 0
0 0 0 0 0 1 0 0 0 1 1 0 1 0 1 0 0
0 0 0 0 0 1 0 0 0 1 1 1 1 0 1 1 0
0 0 0 0 0 1 0 0 1 0 0 0 1 1 0 0 0
0 0 0 0 0 1 0 0 1 0 0 1 1 1 0 1 0
0 0 0 0 0 1 0 0 1 0 1 0 1 1 1 0 0
0 0 0 0 0 1 0 0 1 0 1 1 1 1 1 1 0
0 0 0 0 0 1 0 0 1 1 0 0 0 0 0 0 1
0 0 0 0 0 1 0 0 1 1 0 1 0 0 0 1 1
0 0 0 0 0 1 0 0 1 1 1 0 0 0 1 0 1
0 0 0 0 0 1 0 0 1 1 1 1 0 0 1 1 1
0 0 0 0 0 1 0 1 0 0 0 0 0 1 0 1 0
0 0 0 0 0 1 0 1 0 0 0 1 0 1 1 0 0
0 0 0 0 0 1 0 1 0 0 1 0 0 1 1 1 0
0 0 0 0 0 1 0 1 0 0 1 1 1 0 0 0 0
0 0 0 0 0 1 0 1 0 1 0 0 1 0 0 1 0
0 0 0 0 0 1 0 1 0 1 0 1 1 0 1 0 0
0 0 0 0 0 1 0 1 0 1 1 0 1 0 1 1 0
0 0 0 0 0 1 0 1 0 1 1 1 1 1 0 0 0
0 0 0 0 0 1 0 1 1 0 0 0 1 1 0 1 0
0 0 0 0 0 1 0 1 1 0 0 1 1 1 1 0 0
0 0 0 0 0 1 0 1 1 0 1 0 1 1 1 1 0
0 0 0 0 0 1 0 1 1 0 1 1 0 0 0 0 1
0 0 0 0 0 1 0 1 1 1 0 0 0 0 0 1 1
0 0 0 0 0 1 0 1 1 1 0 1 0 0 1 0 1
0 0 0 0 0 1 0 1 1 1 1 0 0 0 1 1 1
0 0 0 0 0 1 0 1 1 1 1 1 0 1 0 0 1
0 0 0 0 0 1 1 0 0 0 0 0 0 1 1 0 0
0 0 0 0 0 1 1 0 0 0 0 1 0 1 1 1 0
0 0 0 0 0 1 1 0 0 0 1 0 1 0 0 0 0
0 0 0 0 0 1 1 0 0 0 1 1 1 0 0 1 0
0 0 0 0 0 1 1 0 0 1 0 0 1 0 1 0 0
0 0 0 0 0 1 1 0 0 1 0 1 1 0 1 1 0
0 0 0 0 0 1 1 0 0 1 1 0 1 1 0 0 0
0 0 0 0 0 1 1 0 0 1 1 1 1 1 0 1 0
0 0 0 0 0 1 1 0 1 0 0 0 1 1 1 0 0
0 0 0 0 0 1 1 0 1 0 0 1 1 1 1 1 0
0 0 0 0 0 1 1 0 1 0 1 0 0 0 0 0 1
0 0 0 0 0 1 1 0 1 0 1 1 0 0 0 1 1
0 0 0 0 0 1 1 0 1 1 0 0 0 0 1 0 1
0 0 0 0 0 1 1 0 1 1 0 1 0 0 1 1 1
0 0 0 0 0 1 1 0 1 1 1 0 0 1 0 0 1
0 0 0 0 0 1 1 0 1 1 1 1 0 1 0 1 1
0 0 0 0 0 1 1 1 0 0 0 0 0 1 1 1 0
0 0 0 0 0 1 1 1 0 0 0 1 1 0 0 0 0
0 0 0 0 0 1 1 1 0 0 1 0 1 0 0 1 0
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*/

/* Test case Shift:
op_0 op_1 op_2 op_3 a_3 a_2 a_1 a_0 b_3 b_2 b_1 b_0 r_3 r_2 r_1 r_0 c_out
0 0 0 1 0 0 0 0 X X X X 0 0 0 0 0
0 0 0 1 0 0 0 1 X X X X 0 0 1 0 0
0 0 0 1 0 0 1 0 X X X X 0 1 0 0 0
0 0 0 1 0 0 1 1 X X X X 0 1 1 0 0
0 0 0 1 0 1 0 0 X X X X 1 0 0 0 0
0 0 0 1 0 1 0 1 X X X X 1 0 1 0 0
0 0 0 1 0 1 1 0 X X X X 1 1 0 0 0
0 0 0 1 0 1 1 1 X X X X 1 1 1 0 0
0 0 0 1 1 0 0 0 X X X X 0 0 0 0 1
0 0 0 1 1 0 0 1 X X X X 0 0 1 0 1
0 0 0 1 1 0 1 0 X X X X 0 1 0 0 1
0 0 0 1 1 0 1 1 X X X X 0 1 1 0 1
0 0 0 1 1 1 0 0 X X X X 1 0 0 0 1
0 0 0 1 1 1 0 1 X X X X 1 0 1 0 1
0 0 0 1 1 1 1 0 X X X X 1 1 0 0 1
0 0 0 1 1 1 1 1 X X X X 1 1 1 0 1
*/

/* Test case AND:
op_0 op_1 op_2 op_3 a_3 a_2 a_1 a_0 b_3 b_2 b_1 b_0 r_3 r_2 r_1 r_0 c_out
0 0 1 0 0 0 0 0 0 0 0 0 0 0 0 0 0
0 0 1 0 0 0 0 0 0 0 0 1 0 0 0 0 0
0 0 1 0 0 0 0 0 0 0 1 0 0 0 0 0 0
0 0 1 0 0 0 0 0 0 0 1 1 0 0 0 0 0
0 0 1 0 0 0 0 0 0 1 0 0 0 0 0 0 0
0 0 1 0 0 0 0 0 0 1 0 1 0 0 0 0 0
0 0 1 0 0 0 0 0 0 1 1 0 0 0 0 0 0
0 0 1 0 0 0 0 0 0 1 1 1 0 0 0 0 0
0 0 1 0 0 0 0 0 1 0 0 0 0 0 0 0 0
0 0 1 0 0 0 0 0 1 0 0 1 0 0 0 0 0
0 0 1 0 0 0 0 0 1 0 1 0 0 0 0 0 0
0 0 1 0 0 0 0 0 1 0 1 1 0 0 0 0 0
0 0 1 0 0 0 0 0 1 1 0 0 0 0 0 0 0
0 0 1 0 0 0 0 0 1 1 0 1 0 0 0 0 0
0 0 1 0 0 0 0 0 1 1 1 0 0 0 0 0 0
0 0 1 0 0 0 0 0 1 1 1 1 0 0 0 0 0
0 0 1 0 0 0 0 1 0 0 0 0 0 0 0 0 0
0 0 1 0 0 0 0 1 0 0 0 1 0 0 0 1 0
0 0 1 0 0 0 0 1 0 0 1 0 0 0 0 0 0
0 0 1 0 0 0 0 1 0 0 1 1 0 0 0 1 0
0 0 1 0 0 0 0 1 0 1 0 0 0 0 0 0 0
0 0 1 0 0 0 0 1 0 1 0 1 0 0 0 1 0
0 0 1 0 0 0 0 1 0 1 1 0 0 0 0 0 0
0 0 1 0 0 0 0 1 0 1 1 1 0 0 0 1 0
0 0 1 0 0 0 0 1 1 0 0 0 0 0 0 0 0
0 0 1 0 0 0 0 1 1 0 0 1 0 0 0 1 0
0 0 1 0 0 0 0 1 1 0 1 0 0 0 0 0 0
0 0 1 0 0 0 0 1 1 0 1 1 0 0 0 1 0
0 0 1 0 0 0 0 1 1 1 0 0 0 0 0 0 0
0 0 1 0 0 0 0 1 1 1 0 1 0 0 0 1 0
0 0 1 0 0 0 0 1 1 1 1 0 0 0 0 0 0
0 0 1 0 0 0 0 1 1 1 1 1 0 0 0 1 0
0 0 1 0 0 0 1 0 0 0 0 0 0 0 0 0 0
0 0 1 0 0 0 1 0 0 0 0 1 0 0 0 0 0
0 0 1 0 0 0 1 0 0 0 1 0 0 0 1 0 0
0 0 1 0 0 0 1 0 0 0 1 1 0 0 1 0 0
0 0 1 0 0 0 1 0 0 1 0 0 0 0 0 0 0
0 0 1 0 0 0 1 0 0 1 0 1 0 0 0 0 0
0 0 1 0 0 0 1 0 0 1 1 0 0 0 1 0 0
0 0 1 0 0 0 1 0 0 1 1 1 0 0 1 0 0
0 0 1 0 0 0 1 0 1 0 0 0 0 0 0 0 0
0 0 1 0 0 0 1 0 1 0 0 1 0 0 0 0 0
0 0 1 0 0 0 1 0 1 0 1 0 0 0 1 0 0
0 0 1 0 0 0 1 0 1 0 1 1 0 0 1 0 0
0 0 1 0 0 0 1 0 1 1 0 0 0 0 0 0 0
0 0 1 0 0 0 1 0 1 1 0 1 0 0 0 0 0
0 0 1 0 0 0 1 0 1 1 1 0 0 0 1 0 0
0 0 1 0 0 0 1 0 1 1 1 1 0 0 1 0 0
0 0 1 0 0 0 1 1 0 0 0 0 0 0 0 0 0
0 0 1 0 0 0 1 1 0 0 0 1 0 0 0 1 0
0 0 1 0 0 0 1 1 0 0 1 0 0 0 1 0 0
0 0 1 0 0 0 1 1 0 0 1 1 0 0 1 1 0
0 0 1 0 0 0 1 1 0 1 0 0 0 0 0 0 0
0 0 1 0 0 0 1 1 0 1 0 1 0 0 0 1 0
0 0 1 0 0 0 1 1 0 1 1 0 0 0 1 0 0
0 0 1 0 0 0 1 1 0 1 1 1 0 0 1 1 0
0 0 1 0 0 0 1 1 1 0 0 0 0 0 0 0 0
0 0 1 0 0 0 1 1 1 0 0 1 0 0 0 1 0
0 0 1 0 0 0 1 1 1 0 1 0 0 0 1 0 0
0 0 1 0 0 0 1 1 1 0 1 1 0 0 1 1 0
0 0 1 0 0 0 1 1 1 1 0 0 0 0 0 0 0
0 0 1 0 0 0 1 1 1 1 0 1 0 0 0 1 0
0 0 1 0 0 0 1 1 1 1 1 0 0 0 1 0 0
0 0 1 0 0 0 1 1 1 1 1 1 0 0 1 1 0
0 0 1 0 0 1 0 0 0 0 0 0 0 0 0 0 0
0 0 1 0 0 1 0 0 0 0 0 1 0 0 0 0 0
0 0 1 0 0 1 0 0 0 0 1 0 0 0 0 0 0
0 0 1 0 0 1 0 0 0 0 1 1 0 0 0 0 0
0 0 1 0 0 1 0 0 0 1 0 0 0 1 0 0 0
0 0 1 0 0 1 0 0 0 1 0 1 0 1 0 0 0
0 0 1 0 0 1 0 0 0 1 1 0 0 1 0 0 0
0 0 1 0 0 1 0 0 0 1 1 1 0 1 0 0 0
0 0 1 0 0 1 0 0 1 0 0 0 0 0 0 0 0
0 0 1 0 0 1 0 0 1 0 0 1 0 0 0 0 0
0 0 1 0 0 1 0 0 1 0 1 0 0 0 0 0 0
0 0 1 0 0 1 0 0 1 0 1 1 0 0 0 0 0
0 0 1 0 0 1 0 0 1 1 0 0 0 1 0 0 0
0 0 1 0 0 1 0 0 1 1 0 1 0 1 0 0 0
0 0 1 0 0 1 0 0 1 1 1 0 0 1 0 0 0
0 0 1 0 0 1 0 0 1 1 1 1 0 1 0 0 0
0 0 1 0 0 1 0 1 0 0 0 0 0 0 0 0 0
0 0 1 0 0 1 0 1 0 0 0 1 0 0 0 1 0
0 0 1 0 0 1 0 1 0 0 1 0 0 0 0 0 0
0 0 1 0 0 1 0 1 0 0 1 1 0 0 0 1 0
0 0 1 0 0 1 0 1 0 1 0 0 0 1 0 0 0
0 0 1 0 0 1 0 1 0 1 0 1 0 1 0 1 0
0 0 1 0 0 1 0 1 0 1 1 0 0 1 0 0 0
0 0 1 0 0 1 0 1 0 1 1 1 0 1 0 1 0
0 0 1 0 0 1 0 1 1 0 0 0 0 0 0 0 0
0 0 1 0 0 1 0 1 1 0 0 1 0 0 0 1 0
0 0 1 0 0 1 0 1 1 0 1 0 0 0 0 0 0
0 0 1 0 0 1 0 1 1 0 1 1 0 0 0 1 0
0 0 1 0 0 1 0 1 1 1 0 0 0 1 0 0 0
0 0 1 0 0 1 0 1 1 1 0 1 0 1 0 1 0
0 0 1 0 0 1 0 1 1 1 1 0 0 1 0 0 0
0 0 1 0 0 1 0 1 1 1 1 1 0 1 0 1 0
0 0 1 0 0 1 1 0 0 0 0 0 0 0 0 0 0
0 0 1 0 0 1 1 0 0 0 0 1 0 0 0 0 0
0 0 1 0 0 1 1 0 0 0 1 0 0 0 1 0 0
0 0 1 0 0 1 1 0 0 0 1 1 0 0 1 0 0
0 0 1 0 0 1 1 0 0 1 0 0 0 1 0 0 0
0 0 1 0 0 1 1 0 0 1 0 1 0 1 0 0 0
0 0 1 0 0 1 1 0 0 1 1 0 0 1 1 0 0
0 0 1 0 0 1 1 0 0 1 1 1 0 1 1 0 0
0 0 1 0 0 1 1 0 1 0 0 0 0 0 0 0 0
0 0 1 0 0 1 1 0 1 0 0 1 0 0 0 0 0
0 0 1 0 0 1 1 0 1 0 1 0 0 0 1 0 0
0 0 1 0 0 1 1 0 1 0 1 1 0 0 1 0 0
0 0 1 0 0 1 1 0 1 1 0 0 0 1 0 0 0
0 0 1 0 0 1 1 0 1 1 0 1 0 1 0 0 0
0 0 1 0 0 1 1 0 1 1 1 0 0 1 1 0 0
0 0 1 0 0 1 1 0 1 1 1 1 0 1 1 0 0
0 0 1 0 0 1 1 1 0 0 0 0 0 0 0 0 0
0 0 1 0 0 1 1 1 0 0 0 1 0 0 0 1 0
0 0 1 0 0 1 1 1 0 0 1 0 0 0 1 0 0
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*/

/* Test case OR:
op_0 op_1 op_2 op_3 a_3 a_2 a_1 a_0 b_3 b_2 b_1 b_0 r_3 r_2 r_1 r_0 c_out
0 1 0 0 0 0 0 0 0 0 0 0 0 0 0 0 0
0 1 0 0 0 0 0 0 0 0 0 1 0 0 0 1 0
0 1 0 0 0 0 0 0 0 0 1 0 0 0 1 0 0
0 1 0 0 0 0 0 0 0 0 1 1 0 0 1 1 0
0 1 0 0 0 0 0 0 0 1 0 0 0 1 0 0 0
0 1 0 0 0 0 0 0 0 1 0 1 0 1 0 1 0
0 1 0 0 0 0 0 0 0 1 1 0 0 1 1 0 0
0 1 0 0 0 0 0 0 0 1 1 1 0 1 1 1 0
0 1 0 0 0 0 0 0 1 0 0 0 1 0 0 0 0
0 1 0 0 0 0 0 0 1 0 0 1 1 0 0 1 0
0 1 0 0 0 0 0 0 1 0 1 0 1 0 1 0 0
0 1 0 0 0 0 0 0 1 0 1 1 1 0 1 1 0
0 1 0 0 0 0 0 0 1 1 0 0 1 1 0 0 0
0 1 0 0 0 0 0 0 1 1 0 1 1 1 0 1 0
0 1 0 0 0 0 0 0 1 1 1 0 1 1 1 0 0
0 1 0 0 0 0 0 0 1 1 1 1 1 1 1 1 0
0 1 0 0 0 0 0 1 0 0 0 0 0 0 0 1 0
0 1 0 0 0 0 0 1 0 0 0 1 0 0 0 1 0
0 1 0 0 0 0 0 1 0 0 1 0 0 0 1 1 0
0 1 0 0 0 0 0 1 0 0 1 1 0 0 1 1 0
0 1 0 0 0 0 0 1 0 1 0 0 0 1 0 1 0
0 1 0 0 0 0 0 1 0 1 0 1 0 1 0 1 0
0 1 0 0 0 0 0 1 0 1 1 0 0 1 1 1 0
0 1 0 0 0 0 0 1 0 1 1 1 0 1 1 1 0
0 1 0 0 0 0 0 1 1 0 0 0 1 0 0 1 0
0 1 0 0 0 0 0 1 1 0 0 1 1 0 0 1 0
0 1 0 0 0 0 0 1 1 0 1 0 1 0 1 1 0
0 1 0 0 0 0 0 1 1 0 1 1 1 0 1 1 0
0 1 0 0 0 0 0 1 1 1 0 0 1 1 0 1 0
0 1 0 0 0 0 0 1 1 1 0 1 1 1 0 1 0
0 1 0 0 0 0 0 1 1 1 1 0 1 1 1 1 0
0 1 0 0 0 0 0 1 1 1 1 1 1 1 1 1 0
0 1 0 0 0 0 1 0 0 0 0 0 0 0 1 0 0
0 1 0 0 0 0 1 0 0 0 0 1 0 0 1 1 0
0 1 0 0 0 0 1 0 0 0 1 0 0 0 1 0 0
0 1 0 0 0 0 1 0 0 0 1 1 0 0 1 1 0
0 1 0 0 0 0 1 0 0 1 0 0 0 1 1 0 0
0 1 0 0 0 0 1 0 0 1 0 1 0 1 1 1 0
0 1 0 0 0 0 1 0 0 1 1 0 0 1 1 0 0
0 1 0 0 0 0 1 0 0 1 1 1 0 1 1 1 0
0 1 0 0 0 0 1 0 1 0 0 0 1 0 1 0 0
0 1 0 0 0 0 1 0 1 0 0 1 1 0 1 1 0
0 1 0 0 0 0 1 0 1 0 1 0 1 0 1 0 0
0 1 0 0 0 0 1 0 1 0 1 1 1 0 1 1 0
0 1 0 0 0 0 1 0 1 1 0 0 1 1 1 0 0
0 1 0 0 0 0 1 0 1 1 0 1 1 1 1 1 0
0 1 0 0 0 0 1 0 1 1 1 0 1 1 1 0 0
0 1 0 0 0 0 1 0 1 1 1 1 1 1 1 1 0
0 1 0 0 0 0 1 1 0 0 0 0 0 0 1 1 0
0 1 0 0 0 0 1 1 0 0 0 1 0 0 1 1 0
0 1 0 0 0 0 1 1 0 0 1 0 0 0 1 1 0
0 1 0 0 0 0 1 1 0 0 1 1 0 0 1 1 0
0 1 0 0 0 0 1 1 0 1 0 0 0 1 1 1 0
0 1 0 0 0 0 1 1 0 1 0 1 0 1 1 1 0
0 1 0 0 0 0 1 1 0 1 1 0 0 1 1 1 0
0 1 0 0 0 0 1 1 0 1 1 1 0 1 1 1 0
0 1 0 0 0 0 1 1 1 0 0 0 1 0 1 1 0
0 1 0 0 0 0 1 1 1 0 0 1 1 0 1 1 0
0 1 0 0 0 0 1 1 1 0 1 0 1 0 1 1 0
0 1 0 0 0 0 1 1 1 0 1 1 1 0 1 1 0
0 1 0 0 0 0 1 1 1 1 0 0 1 1 1 1 0
0 1 0 0 0 0 1 1 1 1 0 1 1 1 1 1 0
0 1 0 0 0 0 1 1 1 1 1 0 1 1 1 1 0
0 1 0 0 0 0 1 1 1 1 1 1 1 1 1 1 0
0 1 0 0 0 1 0 0 0 0 0 0 0 1 0 0 0
0 1 0 0 0 1 0 0 0 0 0 1 0 1 0 1 0
0 1 0 0 0 1 0 0 0 0 1 0 0 1 1 0 0
0 1 0 0 0 1 0 0 0 0 1 1 0 1 1 1 0
0 1 0 0 0 1 0 0 0 1 0 0 0 1 0 0 0
0 1 0 0 0 1 0 0 0 1 0 1 0 1 0 1 0
0 1 0 0 0 1 0 0 0 1 1 0 0 1 1 0 0
0 1 0 0 0 1 0 0 0 1 1 1 0 1 1 1 0
0 1 0 0 0 1 0 0 1 0 0 0 1 1 0 0 0
0 1 0 0 0 1 0 0 1 0 0 1 1 1 0 1 0
0 1 0 0 0 1 0 0 1 0 1 0 1 1 1 0 0
0 1 0 0 0 1 0 0 1 0 1 1 1 1 1 1 0
0 1 0 0 0 1 0 0 1 1 0 0 1 1 0 0 0
0 1 0 0 0 1 0 0 1 1 0 1 1 1 0 1 0
0 1 0 0 0 1 0 0 1 1 1 0 1 1 1 0 0
0 1 0 0 0 1 0 0 1 1 1 1 1 1 1 1 0
0 1 0 0 0 1 0 1 0 0 0 0 0 1 0 1 0
0 1 0 0 0 1 0 1 0 0 0 1 0 1 0 1 0
0 1 0 0 0 1 0 1 0 0 1 0 0 1 1 1 0
0 1 0 0 0 1 0 1 0 0 1 1 0 1 1 1 0
0 1 0 0 0 1 0 1 0 1 0 0 0 1 0 1 0
0 1 0 0 0 1 0 1 0 1 0 1 0 1 0 1 0
0 1 0 0 0 1 0 1 0 1 1 0 0 1 1 1 0
0 1 0 0 0 1 0 1 0 1 1 1 0 1 1 1 0
0 1 0 0 0 1 0 1 1 0 0 0 1 1 0 1 0
0 1 0 0 0 1 0 1 1 0 0 1 1 1 0 1 0
0 1 0 0 0 1 0 1 1 0 1 0 1 1 1 1 0
0 1 0 0 0 1 0 1 1 0 1 1 1 1 1 1 0
0 1 0 0 0 1 0 1 1 1 0 0 1 1 0 1 0
0 1 0 0 0 1 0 1 1 1 0 1 1 1 0 1 0
0 1 0 0 0 1 0 1 1 1 1 0 1 1 1 1 0
0 1 0 0 0 1 0 1 1 1 1 1 1 1 1 1 0
0 1 0 0 0 1 1 0 0 0 0 0 0 1 1 0 0
0 1 0 0 0 1 1 0 0 0 0 1 0 1 1 1 0
0 1 0 0 0 1 1 0 0 0 1 0 0 1 1 0 0
0 1 0 0 0 1 1 0 0 0 1 1 0 1 1 1 0
0 1 0 0 0 1 1 0 0 1 0 0 0 1 1 0 0
0 1 0 0 0 1 1 0 0 1 0 1 0 1 1 1 0
0 1 0 0 0 1 1 0 0 1 1 0 0 1 1 0 0
0 1 0 0 0 1 1 0 0 1 1 1 0 1 1 1 0
0 1 0 0 0 1 1 0 1 0 0 0 1 1 1 0 0
0 1 0 0 0 1 1 0 1 0 0 1 1 1 1 1 0
0 1 0 0 0 1 1 0 1 0 1 0 1 1 1 0 0
0 1 0 0 0 1 1 0 1 0 1 1 1 1 1 1 0
0 1 0 0 0 1 1 0 1 1 0 0 1 1 1 0 0
0 1 0 0 0 1 1 0 1 1 0 1 1 1 1 1 0
0 1 0 0 0 1 1 0 1 1 1 0 1 1 1 0 0
0 1 0 0 0 1 1 0 1 1 1 1 1 1 1 1 0
0 1 0 0 0 1 1 1 0 0 0 0 0 1 1 1 0
0 1 0 0 0 1 1 1 0 0 0 1 0 1 1 1 0
0 1 0 0 0 1 1 1 0 0 1 0 0 1 1 1 0
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*/

/* Test case XOR:
op_0 op_1 op_2 op_3 a_3 a_2 a_1 a_0 b_3 b_2 b_1 b_0 r_3 r_2 r_1 r_0 c_out
0 1 1 0 0 0 0 0 0 0 0 0 0 0 0 0 0
0 1 1 0 0 0 0 0 0 0 0 1 0 0 0 1 0
0 1 1 0 0 0 0 0 0 0 1 0 0 0 1 0 0
0 1 1 0 0 0 0 0 0 0 1 1 0 0 1 1 0
0 1 1 0 0 0 0 0 0 1 0 0 0 1 0 0 0
0 1 1 0 0 0 0 0 0 1 0 1 0 1 0 1 0
0 1 1 0 0 0 0 0 0 1 1 0 0 1 1 0 0
0 1 1 0 0 0 0 0 0 1 1 1 0 1 1 1 0
0 1 1 0 0 0 0 0 1 0 0 0 1 0 0 0 0
0 1 1 0 0 0 0 0 1 0 0 1 1 0 0 1 0
0 1 1 0 0 0 0 0 1 0 1 0 1 0 1 0 0
0 1 1 0 0 0 0 0 1 0 1 1 1 0 1 1 0
0 1 1 0 0 0 0 0 1 1 0 0 1 1 0 0 0
0 1 1 0 0 0 0 0 1 1 0 1 1 1 0 1 0
0 1 1 0 0 0 0 0 1 1 1 0 1 1 1 0 0
0 1 1 0 0 0 0 0 1 1 1 1 1 1 1 1 0
0 1 1 0 0 0 0 1 0 0 0 0 0 0 0 1 0
0 1 1 0 0 0 0 1 0 0 0 1 0 0 0 0 0
0 1 1 0 0 0 0 1 0 0 1 0 0 0 1 1 0
0 1 1 0 0 0 0 1 0 0 1 1 0 0 1 0 0
0 1 1 0 0 0 0 1 0 1 0 0 0 1 0 1 0
0 1 1 0 0 0 0 1 0 1 0 1 0 1 0 0 0
0 1 1 0 0 0 0 1 0 1 1 0 0 1 1 1 0
0 1 1 0 0 0 0 1 0 1 1 1 0 1 1 0 0
0 1 1 0 0 0 0 1 1 0 0 0 1 0 0 1 0
0 1 1 0 0 0 0 1 1 0 0 1 1 0 0 0 0
0 1 1 0 0 0 0 1 1 0 1 0 1 0 1 1 0
0 1 1 0 0 0 0 1 1 0 1 1 1 0 1 0 0
0 1 1 0 0 0 0 1 1 1 0 0 1 1 0 1 0
0 1 1 0 0 0 0 1 1 1 0 1 1 1 0 0 0
0 1 1 0 0 0 0 1 1 1 1 0 1 1 1 1 0
0 1 1 0 0 0 0 1 1 1 1 1 1 1 1 0 0
0 1 1 0 0 0 1 0 0 0 0 0 0 0 1 0 0
0 1 1 0 0 0 1 0 0 0 0 1 0 0 1 1 0
0 1 1 0 0 0 1 0 0 0 1 0 0 0 0 0 0
0 1 1 0 0 0 1 0 0 0 1 1 0 0 0 1 0
0 1 1 0 0 0 1 0 0 1 0 0 0 1 1 0 0
0 1 1 0 0 0 1 0 0 1 0 1 0 1 1 1 0
0 1 1 0 0 0 1 0 0 1 1 0 0 1 0 0 0
0 1 1 0 0 0 1 0 0 1 1 1 0 1 0 1 0
0 1 1 0 0 0 1 0 1 0 0 0 1 0 1 0 0
0 1 1 0 0 0 1 0 1 0 0 1 1 0 1 1 0
0 1 1 0 0 0 1 0 1 0 1 0 1 0 0 0 0
0 1 1 0 0 0 1 0 1 0 1 1 1 0 0 1 0
0 1 1 0 0 0 1 0 1 1 0 0 1 1 1 0 0
0 1 1 0 0 0 1 0 1 1 0 1 1 1 1 1 0
0 1 1 0 0 0 1 0 1 1 1 0 1 1 0 0 0
0 1 1 0 0 0 1 0 1 1 1 1 1 1 0 1 0
0 1 1 0 0 0 1 1 0 0 0 0 0 0 1 1 0
0 1 1 0 0 0 1 1 0 0 0 1 0 0 1 0 0
0 1 1 0 0 0 1 1 0 0 1 0 0 0 0 1 0
0 1 1 0 0 0 1 1 0 0 1 1 0 0 0 0 0
0 1 1 0 0 0 1 1 0 1 0 0 0 1 1 1 0
0 1 1 0 0 0 1 1 0 1 0 1 0 1 1 0 0
0 1 1 0 0 0 1 1 0 1 1 0 0 1 0 1 0
0 1 1 0 0 0 1 1 0 1 1 1 0 1 0 0 0
0 1 1 0 0 0 1 1 1 0 0 0 1 0 1 1 0
0 1 1 0 0 0 1 1 1 0 0 1 1 0 1 0 0
0 1 1 0 0 0 1 1 1 0 1 0 1 0 0 1 0
0 1 1 0 0 0 1 1 1 0 1 1 1 0 0 0 0
0 1 1 0 0 0 1 1 1 1 0 0 1 1 1 1 0
0 1 1 0 0 0 1 1 1 1 0 1 1 1 1 0 0
0 1 1 0 0 0 1 1 1 1 1 0 1 1 0 1 0
0 1 1 0 0 0 1 1 1 1 1 1 1 1 0 0 0
0 1 1 0 0 1 0 0 0 0 0 0 0 1 0 0 0
0 1 1 0 0 1 0 0 0 0 0 1 0 1 0 1 0
0 1 1 0 0 1 0 0 0 0 1 0 0 1 1 0 0
0 1 1 0 0 1 0 0 0 0 1 1 0 1 1 1 0
0 1 1 0 0 1 0 0 0 1 0 0 0 0 0 0 0
0 1 1 0 0 1 0 0 0 1 0 1 0 0 0 1 0
0 1 1 0 0 1 0 0 0 1 1 0 0 0 1 0 0
0 1 1 0 0 1 0 0 0 1 1 1 0 0 1 1 0
0 1 1 0 0 1 0 0 1 0 0 0 1 1 0 0 0
0 1 1 0 0 1 0 0 1 0 0 1 1 1 0 1 0
0 1 1 0 0 1 0 0 1 0 1 0 1 1 1 0 0
0 1 1 0 0 1 0 0 1 0 1 1 1 1 1 1 0
0 1 1 0 0 1 0 0 1 1 0 0 1 0 0 0 0
0 1 1 0 0 1 0 0 1 1 0 1 1 0 0 1 0
0 1 1 0 0 1 0 0 1 1 1 0 1 0 1 0 0
0 1 1 0 0 1 0 0 1 1 1 1 1 0 1 1 0
0 1 1 0 0 1 0 1 0 0 0 0 0 1 0 1 0
0 1 1 0 0 1 0 1 0 0 0 1 0 1 0 0 0
0 1 1 0 0 1 0 1 0 0 1 0 0 1 1 1 0
0 1 1 0 0 1 0 1 0 0 1 1 0 1 1 0 0
0 1 1 0 0 1 0 1 0 1 0 0 0 0 0 1 0
0 1 1 0 0 1 0 1 0 1 0 1 0 0 0 0 0
0 1 1 0 0 1 0 1 0 1 1 0 0 0 1 1 0
0 1 1 0 0 1 0 1 0 1 1 1 0 0 1 0 0
0 1 1 0 0 1 0 1 1 0 0 0 1 1 0 1 0
0 1 1 0 0 1 0 1 1 0 0 1 1 1 0 0 0
0 1 1 0 0 1 0 1 1 0 1 0 1 1 1 1 0
0 1 1 0 0 1 0 1 1 0 1 1 1 1 1 0 0
0 1 1 0 0 1 0 1 1 1 0 0 1 0 0 1 0
0 1 1 0 0 1 0 1 1 1 0 1 1 0 0 0 0
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*/

/* Test case NAND:
op_0 op_1 op_2 op_3 a_3 a_2 a_1 a_0 b_3 b_2 b_1 b_0 r_3 r_2 r_1 r_0 c_out
1 0 1 0 0 0 0 0 0 0 0 0 1 1 1 1 0
1 0 1 0 0 0 0 0 0 0 0 1 1 1 1 1 0
1 0 1 0 0 0 0 0 0 0 1 0 1 1 1 1 0
1 0 1 0 0 0 0 0 0 0 1 1 1 1 1 1 0
1 0 1 0 0 0 0 0 0 1 0 0 1 1 1 1 0
1 0 1 0 0 0 0 0 0 1 0 1 1 1 1 1 0
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*/

/* Test case NOR:
op_0 op_1 op_2 op_3 a_3 a_2 a_1 a_0 b_3 b_2 b_1 b_0 r_3 r_2 r_1 r_0 c_out
1 1 0 0 0 0 0 0 0 0 0 0 1 1 1 1 0
1 1 0 0 0 0 0 0 0 0 0 1 1 1 1 0 0
1 1 0 0 0 0 0 0 0 0 1 0 1 1 0 1 0
1 1 0 0 0 0 0 0 0 0 1 1 1 1 0 0 0
1 1 0 0 0 0 0 0 0 1 0 0 1 0 1 1 0
1 1 0 0 0 0 0 0 0 1 0 1 1 0 1 0 0
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*/

/* Test case NOT:
op_0 op_1 op_2 op_3 a_3 a_2 a_1 a_0 b_3 b_2 b_1 b_0 r_3 r_2 r_1 r_0 c_out
1 1 1 0 0 0 0 0 0 0 0 0 1 1 1 1 0
1 1 1 0 0 0 0 1 0 0 0 0 1 1 1 0 0
1 1 1 0 0 0 1 0 0 0 0 0 1 1 0 1 0
1 1 1 0 0 0 1 1 0 0 0 0 1 1 0 0 0
1 1 1 0 0 1 0 0 0 0 0 0 1 0 1 1 0
1 1 1 0 0 1 0 1 0 0 0 0 1 0 1 0 0
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*/
