// Digital circuit circuit.dig as structural Verilog
module circuit (
  input  P_3,
  input  P_2,
  input  P_1,
  input  P_0,
  input  P_VIP,
  input  A_VIP,
  input  A_3,
  input  A_2,
  input  A_1,
  input  A_0,
  input  CK,
  output y_2,
  output y_1,
  output y_0,
  output z_2,
  output z_1,
  output z_0
);

  wire a, a_t, and_3_out, and_8_out, and_9_out, and_10_out, and_11_out, and_12_out, b, b_t, c, c_t, CK_2, d,
       d_t, DESTINATION, DIR_DOWN, DIR_UP, DOWN, e, e_t, f, f_t, g, g_t, L1_out, L2_out, L3_out, L4_out,
       L5_out, L6_out, not_1_out, not_2_out, R_0, R_1, R_2, R_3, R_VIP, RESET_0, RESET_1, RESET_2, RESET_3,
       RESET_VIP, STOP, t_0, t_1, t_2, t_3, TIMEOUT, UP, WAS_DOWN;
  wire [2:0] rom_1_d;
  wire [7:5] d_ff_1_q;
  wire [15:0] D_1, D_2, D_3, D_4;

  ROM #(.AddrBits(5), .Bits(3)) rom_1 (.A({A_VIP, A_3, A_2, A_1, A_0}), .sel(1'b1), .D(rom_1_d));
  and and_1 (RESET_0, TIMEOUT, ~y_0, ~y_1, ~y_2);  // And
  D_FF #(.Bits(3)) d_ff_1 (.D(rom_1_d), .C(CK_2), .Q(d_ff_1_q));  // open: nQ
  and and_2 (RESET_1, TIMEOUT, y_0, ~y_1, ~y_2);  // And
  and and_3 (and_3_out, z_1, z_0);
  not not_1 (not_1_out, z_1);
  not not_2 (not_2_out, z_0);
  ROM #(.AddrBits(8), .Bits(3)) rom_2 (.A({d_ff_1_q, R_0, R_1, R_2, R_3, R_VIP}), .sel(1'b1), .D({UP, STOP, DOWN}));
  LookUpTable L1 (
    .in0(z_2), .in1(z_1), .in2(z_0), .in3(WAS_DOWN), .in4(UP), .in5(TIMEOUT), .in6(STOP), .in7(R_VIP),
    .in8(DOWN), .in9(DESTINATION), .in10(CK_2), .out(L1_out));
  LookUpTable L2 (
    .in0(z_2), .in1(z_1), .in2(z_0), .in3(WAS_DOWN), .in4(UP), .in5(TIMEOUT), .in6(STOP), .in7(R_VIP),
    .in8(DOWN), .in9(DESTINATION), .in10(CK_2), .out(L2_out));
  LookUpTable L3 (
    .in0(z_2), .in1(z_1), .in2(z_0), .in3(WAS_DOWN), .in4(UP), .in5(TIMEOUT), .in6(STOP), .in7(R_VIP),
    .in8(DOWN), .in9(DESTINATION), .in10(CK_2), .out(L3_out));
  and and_4 (DIR_DOWN, not_2_out, z_1);
  and and_5 (DIR_UP, z_0, not_1_out);
  CounterPreset #(.maxValue(8), .Bits(4)) counterpreset_1 (
    .en(and_3_out), .C(CK), .dir(1'b0), .in(4'b0000), .ld(1'b0), .clr(1'b0), .out({t_3, t_2, t_1, t_0}),
    .ovf(TIMEOUT));
  D_FF Z_2_n (.D(L1_out), .C(CK), .Q(z_2));  // open: nQ
  D_FF Z_1_n (.D(L2_out), .C(CK), .Q(z_1));  // open: nQ
  D_FF Z_0_n (.D(L3_out), .C(CK), .Q(z_0));  // open: nQ
  and and_6 (RESET_2, TIMEOUT, ~y_0, y_1, ~y_2);  // And
  and and_7 (RESET_3, TIMEOUT, y_0, y_1, ~y_2);  // And
  and and_8 (and_8_out, A_0, R_0);
  and and_9 (and_9_out, A_1, R_1);
  and and_10 (and_10_out, A_2, R_2);
  and and_11 (and_11_out, A_3, R_3);
  and and_12 (and_12_out, A_VIP, R_VIP);
  or or_1 (DESTINATION, and_8_out, and_9_out, and_10_out, and_11_out, and_12_out);
  and and_13 (RESET_VIP, TIMEOUT, ~y_0, ~y_1, y_2);  // And
  LookUpTable L4 (.in0(y_2), .in1(y_1), .in2(y_0), .in3(DIR_UP), .in4(DIR_DOWN), .in5(CK_2), .out(L4_out));
  LookUpTable L5 (.in0(y_2), .in1(y_1), .in2(y_0), .in3(DIR_UP), .in4(DIR_DOWN), .in5(CK_2), .out(L5_out));
  LookUpTable L6 (.in0(y_2), .in1(y_1), .in2(y_0), .in3(DIR_UP), .in4(DIR_DOWN), .in5(CK_2), .out(L6_out));
  D_FF Y_2_n (.D(L4_out), .C(CK), .Q(y_2));  // open: nQ
  D_FF Y_1_n (.D(L5_out), .C(CK), .Q(y_1));  // open: nQ
  D_FF Y_0_n (.D(L6_out), .C(CK), .Q(y_0));  // open: nQ
  RS_FF_AS rs_ff_as_1 (.S(P_VIP), .R(RESET_VIP), .Q(R_VIP));  // open: nQ
  RS_FF_AS rs_ff_as_2 (.S(P_3), .R(RESET_3), .Q(R_3));  // open: nQ
  RS_FF_AS rs_ff_as_3 (.S(P_2), .R(RESET_2), .Q(R_2));  // open: nQ
  RS_FF_AS rs_ff_as_4 (.S(P_1), .R(RESET_1), .Q(R_1));  // open: nQ
  RS_FF_AS rs_ff_as_5 (.S(P_0), .R(RESET_0), .Q(R_0));  // open: nQ
  or or_2 (CK_2, A_VIP, A_3, A_2, A_1, A_0);
  RS_FF_AS rs_ff_as_6 (.S(DIR_DOWN), .R(~DOWN), .Q(WAS_DOWN));  // open: nQ
  Seven_Seg #(.commonCathode("true")) seven_seg_1 (
    .a(a), .b(b), .c(c), .d(d), .e(e), .f(f), .g(g), .dp(1'b0), .common(1'b0));
  SixteenSeg sixteenseg_1 (.led(D_1), .dp(1'b0));
  SixteenSeg sixteenseg_2 (.led(D_2), .dp(1'b0));
  SixteenSeg sixteenseg_3 (.led(D_3), .dp(1'b0));
  ROM #(.AddrBits(3), .Bits(7)) rom_3 (.A({y_2, y_1, y_0}), .sel(1'b1), .D({a, b, c, d, e, f, g}));
  SixteenSeg sixteenseg_4 (.led(D_4), .dp(1'b0));
  Seven_Seg #(.commonCathode("true")) seven_seg_2 (
    .a(a_t), .b(b_t), .c(c_t), .d(d_t), .e(e_t), .f(f_t), .g(g_t), .dp(1'b0), .common(1'b0));
  ROM #(.AddrBits(3), .Bits(32)) rom_4 (.A({z_2, z_1, z_0}), .sel(1'b1), .D({D_2, D_1}));
  ROM #(.AddrBits(3), .Bits(32)) rom_5 (.A({z_2, z_1, z_0}), .sel(1'b1), .D({D_4, D_3}));
  ROM #(.AddrBits(4), .Bits(7)) rom_6 (.A({t_3, t_2, t_1, t_0}), .sel(1'b1), .D({a_t, b_t, c_t, d_t, e_t, f_t, g_t}));

  // Other names for the same wires on the sheet: Z_0_n = z_0; Z_1_n = z_1; Z_2_n = z_2

  // Notes on the sheet:
  //   Requests Management
  //   FSM states
  //   Arrival signal encoder
  //   Reset Management
  //   contents of rom_1 (hex, n*v repeats v):
  //   0,0,1,0,2,0,0,0,3,7*0,4
  //   Arrival signal storage
  //   Comparator
  //   contents of rom_2 (hex, n*v repeats v):
  //   0,15*4,2,15*6,0,7*4,2,7*6,1,7*5,3,7*7,0,4,4,4,2,6,6,6,1,5,5,5
  //   ,3,7,7,7,1,5,5,5,3,7,7,7,1,5,5,5,3,7,7,7,0,4,2,6,1,5,3,7,1,5,3
  //   ,7,1,5,3,7,1,5,3,7,1,5,3,7,1,5,3,7,1,5,3,7,0,2,1,3,1,3,1,3,1,3
  //   ,1,3,1,3,1,3,1,3,1,3,1,3,1,3,1,3,1,3,1,3,1,3,92*0,1,1,1
  //   contents of L1 (hex, n*v repeats v):
  //   0,1,0,1,0,1,0,1,0,1,0,1,0,1,0,1,0,1,0,1,0,1,0,1,0,1,0,1,0,1,0
  //   ,1,0,1,0,1,0,1,0,1,0,1,0,1,0,1,0,1,0,1,0,1,0,1,0,1,0,1,0,1,0,1
  //   ,0,1,33*0,1,0,1,0,1,0,1,0,1,0,1,0,1,0,1,0,1,0,1,0,1,0,1,0,1,0
  //   ,1,0,1,0,1,0,1,0,1,0,1,0,1,0,1,0,1,0,1,0,1,0,1,0,1,0,1,0,1,0,1
  //   ,0,1,0,1,0,1,0,1,0,1,0,1,0,1,0,1,0,1,0,1,0,1,0,1,0,1,0,1,0,1,0
  //   ,1,0,1,0,1,0,1,33*0,1,0,1,0,1,0,1,0,1,0,1,0,1,0,1,0,1,0,1,0,1
  //   ,0,1,0,1,0,1,0,1,0,1,0,1,0,1,0,1,0,1,0,1,0,1,0,1,0,1,0,1,0,1,0
  //   ,1,0,1,0,1,0,1,0,1,0,1,0,1,0,1,0,1,0,1,0,1,0,1,0,1,0,1,0,1,0,1
  //   ,0,1,0,1,0,1,0,1,0,1,0,1,33*0,1,0,1,0,1,0,1,0,1,0,1,0,1,0,1,0
  //   ,1,0,1,0,1,0,1,0,1,0,1,0,1,0,1,0,1,0,1,0,1,0,1,0,1,0,1,0,1,0,1
  //   ,0,1,0,1,0,1,0,1,0,1,0,1,0,1,0,1,0,1,0,1,0,1,0,1,0,1,0,1,0,1,0
  //   ,1,0,1,0,1,0,1,0,1,0,1,0,1,0,1,0,1,33*0,1,0,1,0,1,0,1,0,1,0,1
  //   ,0,1,0,1,0,1,0,1,0,1,0,1,0,1,0,1,0,1,0,1,0,1,0,1,0,1,0,1,0,1,0
  //   ,1,0,1,0,1,0,1,0,1,0,1,0,1,0,1,0,1,0,1,0,1,0,1,0,1,0,1,0,1,0,1
  //   ,0,1,0,1,0,1,0,1,0,1,0,1,0,1,0,1,0,1,0,1,0,1,33*0,1,0,1,0,1,0
  //   ,1,0,1,0,1,0,1,0,1,0,1,0,1,0,1,0,1,0,1,0,1,0,1,0,1,0,1,0,1,0,1
  //   ,0,1,0,1,0,1,0,1,0,1,0,1,0,1,0,1,0,1,0,1,0,1,0,1,0,1,0,1,0,1,0
  //   ,1,0,1,0,1,0,1,0,1,0,1,0,1,0,1,0,1,0,1,0,1,0,1,0,1,0,1,33*0,1
  //   ,0,1,0,1,0,1,0,1,0,1,0,1,0,1,0,1,0,1,0,1,0,1,0,1,0,1,0,1,0,1,0
  //   ,1,0,1,0,1,0,1,0,1,0,1,0,1,0,1,0,1,0,1,0,1,0,1,0,1,0,1,0,1,0,1
  //   ,0,1,0,1,0,1,0,1,0,1,0,1,0,1,0,1,0,1,0,1,0,1,0,1,0,1,0,1,0,1,0
  //   ,1,4*0,1,1,6*0,1,1,19*0,1,0,1,0,1,0,1,0,1,0,1,0,1,0,1,0,1,0,1
  //   ,0,1,0,1,0,1,0,1,0,1,0,1,0,1,0,1,0,1,0,1,0,1,0,1,0,1,0,1,0,1,0
  //   ,1,0,1,0,1,0,1,0,1,0,1,0,1,0,1,0,1,0,1,0,1,0,1,0,1,0,1,0,1,0,1
  //   ,0,1,0,1,0,1,0,1,0,1,0,1,0,1,33*0,1,0,1,0,1,0,1,0,1,0,1,0,1,0
  //   ,1,0,1,0,1,0,1,0,1,0,1,0,1,0,1,0,1,0,1,0,1,0,1,0,1,0,1,0,1,0,1
  //   ,0,1,0,1,0,1,0,1,0,1,0,1,0,1,0,1,0,1,0,1,0,1,0,1,0,1,0,1,0,1,0
  //   ,1,0,1,0,1,0,1,0,1,0,1,0,1,0,1,0,1,0,1,33*0,1,0,1,0,1,0,1,0,1
  //   ,0,1,0,1,0,1,0,1,0,1,0,1,0,1,0,1,0,1,0,1,0,1,0,1,0,1,0,1,0,1,0
  //   ,1,0,1,0,1,0,1,0,1,0,1,0,1,0,1,0,1,0,1,0,1,0,1,0,1,0,1,0,1,0,1
  //   ,0,1,0,1,0,1,0,1,0,1,0,1,0,1,0,1,0,1,0,1,0,1,0,1,33*0,1,0,1,0
  //   ,1,0,1,0,1,0,1,0,1,0,1,0,1,0,1,0,1,0,1,0,1,0,1,0,1,0,1,0,1,0,1
  //   ,0,1,0,1,0,1,0,1,0,1,0,1,0,1,0,1,0,1,0,1,0,1,0,1,0,1,0,1,0,1,0
  //   ,1,0,1,0,1,0,1,0,1,0,1,0,1,0,1,0,1,0,1,0,1,0,1,0,1,0,1,0,1,33*0
  //   ,1,0,1,0,1,0,1,0,1,0,1,0,1,0,1,0,1,0,1,0,1,0,1,0,1,0,1,0,1,0,1
  //   ,0,1,0,1,0,1,0,1,0,1,0,1,0,1,0,1,0,1,0,1,0,1,0,1,0,1,0,1,0,1,0
  //   ,1,0,1,0,1,0,1,0,1,0,1,0,1,0,1,0,1,0,1,0,1,0,1,0,1,0,1,0,1,0,1
  //   ,0,1,26*0,1,1,5*0,1,0,1,0,1,0,1,0,1,0,1,0,1,0,1,0,1,0,1,0,1,0
  //   ,1,0,1,1,1,0,1,0,1,0,1,0,1,0,1,0,1,0,1,0,1,0,1,0,1,0,1,0,1,0,1
  //   ,0,1,0,1,0,1,0,1,0,1,0,1,0,1,0,1,0,1,0,1,0,1,0,1,0,1,0,1,0,1,0
  //   ,1,0,1,0,1,0,1,0,1,0,1,0,0,4*1,4*0,4*1,4*0,4*1,4*0,4*1,0,0,0,5*1
  //   ,0,1,0,5*1,0,1,0,1,1,1,0,1,0,1,0,1,1,1,0,1,0,1,0,1,0,1,0,1,0,1
  //   ,0,1,0,1,0,1,0,1,0,1,0,1,0,1,0,1,0,1,0,1,0,1,0,1,0,1,0,1,0,1,0
  //   ,1,0,1,0,1,0,1,0,1,0,1,0,1,0,1,0,1,0,1,0,1,0,1,0,1,0,0,4*1,4*0
  //   ,4*1,4*0,1,1,6*0,1,1,5*0,5*1,0,1,0,5*1,0,1,0,1,1,1,0,1,0,1,0,1,1,1
  //   ,0,1,0,1,0,1,0,1,0,1,0,1,0,1,0,1,0,1,0,1,0,1,0,1,0,1,0,1,0,1,0
  //   ,1,0,1,0,1,0,1,0,1,0,1,0,1,0,1,0,1,0,1,0,1,0,1,0,1,0,1,0,1,0,1
  //   ,0,1,0,1,0,1,0,0,4*1,4*0,4*1,4*0,4*1,4*0,4*1,0,0,0,1,1,1,0,1,0
  //   ,1,0,1,1,1,0,1,0,1,0,5*1,0,1,0,5*1,0,1,0,1,0,1,0,1,0,1,0,1,0,1
  //   ,0,1,0,1,0,1,0,1,0,1,0,1,0,1,0,1,0,1,0,1,0,1,0,1,0,1,0,1,0,1,0
  //   ,1,0,1,0,1,0,1,0,1,0,1,0,1,0,1,0,1,0,1,0,1,0,0,4*1,4*0,4*1,12*0
  //   ,1,1,5*0,5*1,0,1,0,5*1,0,1,0,1,0,1,0,1,0,1,0,1,1,1,0,1,0,1
  //   contents of L2 (hex, n*v repeats v):
  //   0,0,1,1,0,0,1,1,0,0,1,1,0,0,1,1,0,0,1,1,0,0,1,1,0,0,1,1,0,0,1,1
  //   ,0,0,1,1,6*0,1,1,6*0,1,1,6*0,1,1,4*0,4*1,0,7*1,0,1,1,1,0,1,1,1
  //   ,0,1,1,1,0,1,1,1,0,1,1,1,0,0,1,1,0,0,1,1,0,0,1,1,0,0,1,1,0,0,1,1
  //   ,0,0,1,1,0,0,1,1,0,0,1,1,0,0,1,1,0,0,1,1,0,0,1,1,0,0,1,1,0,0,1,1
  //   ,0,0,1,1,0,0,1,1,0,0,1,1,0,0,1,1,6*0,1,1,6*0,1,1,6*0,1,1,4*0,4*1
  //   ,0,7*1,0,1,1,1,0,1,1,1,0,1,1,1,0,1,1,1,0,1,1,1,0,0,1,1,0,0,1,1
  //   ,0,0,1,1,0,0,1,1,0,0,1,1,0,0,1,1,0,0,1,1,0,0,1,1,1,0,1,1,0,0,1,1,1
  //   ,0,1,1,0,0,1,1,0,0,1,1,0,0,1,1,0,0,1,1,0,0,1,1,0,0,1,1,0,0,1,1
  //   ,0,0,1,1,0,0,1,1,0,0,1,1,6*0,1,1,0,0,1,1,0,1,1,1,0,1,1,1,0,1,1,1
  //   ,0,1,1,1,0,1,1,1,0,1,1,1,0,1,1,1,0,1,1,1,0,0,1,1,6*0,1,1,6*0,1,1
  //   ,6*0,1,1,0,0,1,1,1,0,1,1,0,0,1,1,1,0,1,1,0,0,1,1,0,0,1,1,0,0,1,1
  //   ,0,0,1,1,0,0,1,1,0,0,1,1,0,0,1,1,0,0,1,1,0,0,1,1,0,0,1,1,6*0,1,1
  //   ,5*0,1,1,1,0,1,1,1,0,1,1,1,0,1,1,1,0,1,1,1,0,1,1,1,0,1,1,1,0,1,1,1
  //   ,0,0,1,1,0,0,1,1,0,0,1,1,0,0,1,1,0,0,1,1,0,0,1,1,0,0,1,1,0,0,1,1
  //   ,0,0,1,1,0,0,1,1,0,0,1,1,0,0,1,1,0,0,1,1,0,0,1,1,0,0,1,1,0,0,1,1
  //   ,0,0,1,1,6*0,1,1,6*0,1,1,6*0,1,1,4*0,4*1,0,7*1,0,1,1,1,0,1,1,1
  //   ,0,1,1,1,0,1,1,1,0,1,1,1,0,0,1,1,0,0,1,1,0,0,1,1,0,0,1,1,0,0,1,1
  //   ,0,0,1,1,0,0,1,1,0,0,1,1,0,0,1,1,0,0,1,1,0,0,1,1,0,0,1,1,0,0,1,1
  //   ,0,0,1,1,0,0,1,1,0,0,1,1,0,0,1,1,6*0,1,1,6*0,1,1,6*0,1,1,4*0,4*1
  //   ,0,7*1,0,1,1,1,0,1,1,1,0,1,1,1,0,1,1,1,0,1,1,1,0,0,1,1,0,0,1,1
  //   ,0,0,1,1,0,0,1,1,0,0,1,1,0,0,1,1,0,0,1,1,0,0,1,1,1,0,1,1,0,0,1,1,1
  //   ,0,1,1,0,0,1,1,0,0,1,1,0,0,1,1,0,0,1,1,0,0,1,1,0,0,1,1,0,0,1,1
  //   ,0,0,1,1,0,0,1,1,0,0,1,1,6*0,1,1,0,0,1,1,0,1,1,1,0,1,1,1,0,1,1,1
  //   ,0,1,1,1,0,1,1,1,0,1,1,1,0,1,1,1,0,1,1,1,0,0,1,1,6*0,1,1,6*0,1,1
  //   ,6*0,1,1,0,0,1,1,1,0,1,1,0,0,1,1,1,0,1,1,0,0,1,1,0,0,1,1,0,0,1,1
  //   ,0,0,1,1,0,0,1,1,0,0,1,1,0,0,1,1,0,0,1,1,0,0,1,1,0,0,1,1,6*0,1,1
  //   ,5*0,1,1,1,0,1,1,1,0,1,1,1,0,1,1,1,0,1,1,1,0,1,1,1,0,1,1,1,0,1,1,1
  //   ,0,0,1,1,0,0,1,1,0,0,1,1,0,0,1,1,0,0,1,1,0,0,1,1,0,0,1,1,0,0,1,1
  //   ,0,0,1,1,0,0,1,1,0,0,1,1,0,0,1,1,0,0,1,1,0,0,1,1,0,0,1,1,0,0,1,1
  //   ,0,0,1,1,0,0,1,1,0,0,1,1,0,0,1,1,0,0,1,1,6*0,1,1,5*0,1,1,1,0,1,1,1
  //   ,0,1,1,1,0,1,1,1,0,1,1,1,0,1,1,1,0,1,1,1,0,1,1,1,0,0,1,1,0,0,1,1
  //   ,0,0,1,1,0,0,1,1,0,0,1,1,0,0,1,1,0,0,1,1,0,0,1,1,0,0,1,1,0,0,1,1
  //   ,0,0,1,1,0,0,1,1,0,0,1,1,0,0,1,1,0,0,1,1,0,0,1,1,0,0,1,1,0,0,1,1
  //   ,0,0,1,1,0,0,1,1,0,0,1,1,6*0,1,1,5*0,1,1,1,0,1,1,1,0,1,1,1,0,1,1,1
  //   ,0,1,1,1,0,1,1,1,0,1,1,1,0,1,1,1,0,0,1,1,0,0,1,1,0,0,1,1,0,0,1,1
  //   ,0,0,1,1,0,0,1,1,0,0,1,1,0,0,1,1,1,0,1,1,0,0,1,1,1,0,1,1,0,0,1,1
  //   ,0,0,1,1,0,0,1,1,0,0,1,1,0,0,1,1,0,0,1,1,0,0,1,1,0,0,1,1,0,0,1,1
  //   ,0,0,1,1,6*0,1,1,0,0,1,1,0,1,1,1,0,1,1,1,0,1,1,1,0,1,1,1,0,1,1,1
  //   ,0,1,1,1,0,1,1,1,0,1,1,1,0,0,1,1,6*0,1,1,6*0,1,1,6*0,1,1,0,0,1,1,1
  //   ,0,1,1,0,0,1,1,1,0,1,1,0,0,1,1,0,0,1,1,0,0,1,1,0,0,1,1,0,0,1,1
  //   ,0,0,1,1,0,0,1,1,0,0,1,1,0,0,1,1,0,0,1,1,6*0,1,1,5*0,1,1,1,0,1,1,1
  //   ,0,1,1,1,0,1,1,1,0,1,1,1,0,1,1,1,0,1,0,1,0,1,1,1,0,0,1,1,0,0,1,1
  //   ,0,0,1,1,0,0,1,1,0,0,1,1,0,0,1,1,6*0,1,1,0,0,1,1,0,0,1,1,0,0,1,1
  //   ,0,0,1,1,0,0,1,1,0,0,1,1,0,0,1,1,0,0,1,1,0,0,1,1,0,0,1,1,0,0,1,1
  //   ,0,0,1,1,0,0,1,1,6*0,1,1,5*0,1,0,1,0,1,1,1,0,1,0,1,0,1,1,1,0,1
  //   ,0,1,0,1,1,1,0,1,0,1,0,1,1,1,6*0,1,1,6*0,1,1,6*0,1,1,6*0,1,1,0,0
  //   ,1,1,0,0,1,1,0,0,1,1,0,0,1,1,0,0,1,1,0,0,1,1,0,0,1,1,0,0,1,1,0,0
  //   ,1,1,0,0,1,1,0,0,1,1,0,0,1,1,0,0,1,1,6*0,1,1,5*0,1,0,1,0,1,1,1
  //   ,0,1,0,1,0,1,1,1,0,1,0,1,0,1,1,1,0,1,0,1,0,1,1,1,6*0,1,1,6*0,1,1
  //   ,6*0,1,1,6*0,1,1,1,0,1,1,0,0,1,1,1,0,1,1,0,0,1,1,0,0,1,1,0,0,1,1
  //   ,0,0,1,1,0,0,1,1,0,0,1,1,0,0,1,1,0,0,1,1,0,0,1,1,0,0,1,1,6*0,1,1
  //   ,0,0,1,1,0,1,0,1,0,1,1,1,0,1,0,1,0,1,1,1,0,1,0,1,0,1,1,1,0,1,0
  //   ,1,0,1,1,1,30*0,1,1,1,0,1,1,0,0,1,1,1,0,1,1,0,0,1,1,0,0,1,1,0,0
  //   ,1,1,0,0,1,1,0,0,1,1,0,0,1,1,0,0,1,1,0,0,1,1,0,0,1,1,0,0,1,1,6*0
  //   ,1,1,5*0,1,0,1,0,1,1,1,0,1,0,1,0,1,1,1,0,1,1,1,0,1,1,1,0,1,0,1
  //   ,0,1,1,1,6*0,1,1,6*0,1,1,0,0,1,1,0,0,1,1,6*0,1,1
  //   contents of L3 (hex, n*v repeats v):
  //   4*0,4*1,4*0,5*1,0,0,0,5*1,0,0,0,4*1,4*0,1,1,6*0,1,1,6*0,4*1,4*0
  //   ,6*1,0,7*1,0,5*1,0,1,0,5*1,0,1,0,5*1,4*0,4*1,4*0,4*1,4*0,4*1,4*0
  //   ,4*1,4*0,4*1,4*0,5*1,0,0,0,5*1,0,0,0,4*1,4*0,1,1,6*0,1,1,6*0,4*1
  //   ,4*0,6*1,0,7*1,0,5*1,0,1,0,5*1,0,1,0,5*1,4*0,4*1,4*0,4*1,4*0,4*1
  //   ,4*0,4*1,4*0,4*1,4*0,4*1,4*0,4*1,4*0,4*1,4*0,1,1,6*0,1,1,6*0,4*1
  //   ,4*0,1,1,0,0,0,1,0,5*1,0,1,0,5*1,0,1,0,5*1,0,1,0,5*1,4*0,4*1,4*0
  //   ,4*1,4*0,4*1,4*0,4*1,4*0,4*1,4*0,4*1,4*0,4*1,4*0,4*1,4*0,1,1,6*0
  //   ,1,1,6*0,4*1,4*0,4*1,0,1,0,5*1,0,1,0,5*1,0,1,0,5*1,0,1,0,5*1,4*0
  //   ,4*1,4*0,4*1,4*0,4*1,4*0,4*1,4*0,4*1,4*0,5*1,0,0,0,5*1,0,0,0,4*1
  //   ,4*0,1,1,6*0,1,1,6*0,4*1,4*0,6*1,0,7*1,0,5*1,0,1,0,5*1,0,1,0,5*1
  //   ,4*0,4*1,4*0,4*1,4*0,4*1,4*0,4*1,4*0,4*1,4*0,5*1,0,0,0,5*1,0,0,0
  //   ,4*1,4*0,1,1,6*0,1,1,6*0,4*1,4*0,6*1,0,7*1,0,5*1,0,1,0,5*1,0,1
  //   ,0,5*1,4*0,4*1,4*0,4*1,4*0,4*1,4*0,4*1,4*0,4*1,4*0,4*1,4*0,4*1
  //   ,4*0,4*1,4*0,1,1,6*0,1,1,6*0,4*1,4*0,1,1,0,0,0,1,0,1,0,1,1,1,0
  //   ,1,0,1,0,1,1,1,0,1,0,5*1,0,1,0,5*1,4*0,4*1,4*0,4*1,4*0,4*1,4*0
  //   ,4*1,4*0,4*1,4*0,4*1,4*0,4*1,4*0,4*1,4*0,1,1,6*0,1,1,6*0,4*1,4*0
  //   ,4*1,0,1,0,5*1,0,1,0,5*1,0,1,0,5*1,0,1,0,5*1,4*0,4*1,4*0,4*1,4*0
  //   ,4*1,4*0,4*1,4*0,4*1,4*0,5*1,0,0,0,5*1,0,0,0,4*1,4*0,4*1,4*0,4*1
  //   ,4*0,4*1,4*0,4*1,0,1,0,5*1,0,1,0,5*1,0,1,0,5*1,0,1,0,5*1,4*0,4*1
  //   ,4*0,4*1,4*0,4*1,4*0,4*1,4*0,4*1,4*0,5*1,0,0,0,5*1,0,0,0,4*1,4*0
  //   ,4*1,4*0,4*1,4*0,4*1,4*0,4*1,0,1,0,5*1,0,1,0,5*1,0,1,0,5*1,0,1
  //   ,0,5*1,4*0,4*1,4*0,4*1,4*0,4*1,4*0,4*1,4*0,4*1,4*0,4*1,4*0,4*1
  //   ,4*0,4*1,4*0,1,1,6*0,1,1,6*0,4*1,4*0,1,1,0,0,0,1,0,5*1,0,1,0,5*1
  //   ,0,1,0,5*1,0,1,0,5*1,4*0,4*1,4*0,4*1,4*0,4*1,4*0,4*1,4*0,4*1,4*0
  //   ,4*1,4*0,4*1,4*0,4*1,4*0,1,1,6*0,1,1,6*0,4*1,4*0,4*1,0,1,0,5*1
  //   ,0,1,0,5*1,0,1,0,5*1,0,1,0,5*1,4*0,4*1,4*0,4*1,4*0,4*1,4*0,4*1
  //   ,4*0,4*1,4*0,5*1,0,0,0,5*1,0,0,0,4*1,4*0,4*1,4*0,4*1,4*0,4*1,4*0
  //   ,4*1,0,1,0,1,0,1,1,1,0,1,0,1,0,1,1,1,0,1,0,1,0,1,1,1,0,1,0,1,0
  //   ,1,1,1,6*0,1,1,6*0,1,1,4*0,4*1,4*0,4*1,4*0,4*1,4*0,5*1,0,0,0,5*1
  //   ,0,0,0,4*1,4*0,4*1,4*0,4*1,4*0,4*1,4*0,4*1,0,1,0,1,0,1,1,1,0,1
  //   ,0,1,0,1,1,1,0,1,0,5*1,0,1,0,5*1,6*0,1,1,6*0,1,1,4*0,4*1,4*0,4*1
  //   ,4*0,4*1,4*0,4*1,4*0,4*1,4*0,4*1,4*0,1,1,6*0,1,1,6*0,4*1,4*0,1,1
  //   ,0,0,0,1,0,1,0,1,1,1,0,1,0,1,0,1,1,1,0,1,0,1,0,1,1,1,0,1,0,1,0
  //   ,1,1,1,4*0,4*1,4*0,4*1,6*0,1,1,6*0,1,1,4*0,4*1,4*0,4*1,4*0,4*1
  //   ,4*0,4*1,4*0,1,1,6*0,1,1,6*0,4*1,4*0,4*1,0,1,0,1,0,1,1,1,0,1,0
  //   ,1,0,1,1,1,0,1,0,5*1,0,1,0,5*1,6*0,1,1,6*0,1,1,4*0,4*1,4*0,4*1
  //   Destination arrival signal
  //   FSM floor
  //   contents of L4 (hex, n*v repeats v):
  //   0,1,0,1,0,1,0,1,0,1,0,1,0,1,0,1,0,1,0,1,0,1,0,1,0,1,0,1,0,1,0
  //   ,1,0,1,0,1,0,1,0,1,0,1,0,1,0,1,1,1,9*0,1,0,1,0,1,0,1
  //   contents of L5 (hex, n*v repeats v):
  //   0,0,1,1,0,0,1,1,0,0,1,1,0,0,1,1,0,0,1,1,0,0,1,1,0,0,1,1,0,0,1,1
  //   ,0,0,1,1,0,0,1,1,0,0,4*1,0,0,0,1,0,1,0,1,1,1,0,0,1,1,0,0,1,1
  //   contents of L6 (hex, n*v repeats v):
  //   4*0,4*1,4*0,4*1,4*0,4*1,4*0,4*1,4*0,5*1,0,1,6*0,1,1,1,0,1,0,1
  //   ,4*0,4*1
  //   Pending requests
  //   Floor detector
  //   Direction storage (one for duality)
  //   Call buttons
  //   Arrival at the floor
  //   Current floor
  //   Elevator state
  //   Decoder of 7 segment display
  //   contents of rom_3 (hex, n*v repeats v):
  //   7e,30,6d,79,33
  //   Decoder of 16 segment displays
  //   Timer
  //   contents of rom_4 (hex, n*v repeats v):
  //   3cfa8cc,3c700fc,ff483f,3c700ff,4803063b
  //   contents of rom_5 (hex, n*v repeats v):
  //   48034833,0,24cca8cc,24cc03f3,3c700ff
  //   contents of rom_6 (hex, n*v repeats v):
  //   7e,30,6d,79,33,5b,5f,70,7f
endmodule

/* Test case porte:
CK P_0 P_1 P_2 P_3 P_VIP A_0 A_1 A_2 A_3 A_VIP y_2 y_1 y_0 z_2 z_1 z_0
0  1   0   0   0   0     0   0   0   0   0     0   0   0   0   0   0  
C  0   0   0   0   0     0   0   0   0   0     0   0   0   0   1   1  
C  0   0   0   0   0     0   0   0   0   0     0   0   0   0   1   1  
C  0   0   0   0   0     0   0   0   0   0     0   0   0   0   1   1  
C  0   0   0   0   0     0   0   0   0   0     0   0   0   0   1   1  
C  0   0   0   0   0     0   0   0   0   0     0   0   0   0   1   1  
C  0   0   0   0   0     0   0   0   0   0     0   0   0   0   1   1  
C  0   0   0   0   0     0   0   0   0   0     0   0   0   0   1   1  
C  0   0   0   0   0     0   0   0   0   0     0   0   0   0   1   1  
C  0   0   0   0   0     0   0   0   0   0     0   0   0   0   1   1  
C  0   0   0   0   0     0   0   0   0   0     0   0   0   0   0   0  
*/

/* Test case piani:
CK P_0 P_1 P_2 P_3 P_VIP A_0 A_1 A_2 A_3 A_VIP y_2 y_1 y_0 z_2 z_1 z_0
0  0   1   1   1   0     0   0   0   0   0     0   0   0   0   0   0
C  0   0   0   0   0     0   0   0   0   0     0   0   0   0   0   1
0  0   0   0   0   0     0   1   0   0   0     0   0   0   0   0   1
1  0   0   0   0   0     0   1   0   0   0     0   0   1   1   0   0
C  0   0   0   0   0     0   0   0   0   0     0   0   1   1   0   0  
C  0   0   0   0   0     0   0   0   0   0     0   0   1   0   1   1  
C  0   0   0   0   0     0   0   0   0   0     0   0   1   0   1   1  
C  0   0   0   0   0     0   0   0   0   0     0   0   1   0   1   1  
C  0   0   0   0   0     0   0   0   0   0     0   0   1   0   1   1  
C  0   0   0   0   0     0   0   0   0   0     0   0   1   0   1   1  
C  0   0   0   0   0     0   0   0   0   0     0   0   1   0   1   1  
C  0   0   0   0   0     0   0   0   0   0     0   0   1   0   1   1  
C  0   0   0   0   0     0   0   0   0   0     0   0   1   0   1   1  
C  0   0   0   0   0     0   0   0   0   0     0   0   1   0   1   1  
C  0   0   0   0   0     0   0   0   0   0     0   0   1   0   0   1 
C  0   0   0   0   0     0   0   0   0   0     0   0   1   0   0   1
0  0   0   0   0   0     0   0   1   0   0     0   0   1   0   0   1
1  0   0   0   0   0     0   0   1   0   0     0   1   0   1   0   0
C  0   0   0   0   0     0   0   0   0   0     0   1   0   1   0   0  
C  0   0   0   0   0     0   0   0   0   0     0   1   0   0   1   1  
C  0   0   0   0   0     0   0   0   0   0     0   1   0   0   1   1  
C  0   0   0   0   0     0   0   0   0   0     0   1   0   0   1   1  
C  0   0   0   0   0     0   0   0   0   0     0   1   0   0   1   1  
C  0   0   0   0   0     0   0   0   0   0     0   1   0   0   1   1  
C  0   0   0   0   0     0   0   0   0   0     0   1   0   0   1   1  
C  0   0   0   0   0     0   0   0   0   0     0   1   0   0   1   1  
C  0   0   0   0   0     0   0   0   0   0     0   1   0   0   1   1  
C  0   0   0   0   0     0   0   0   0   0     0   1   0   0   1   1  
C  0   0   0   0   0     0   0   0   0   0     0   1   0   0   0   1 
C  0   0   0   0   0     0   0   0   0   0     0   1   0   0   0   1
0  0   0   0   0   0     0   0   0   1   0     0   1   0   0   0   1
1  0   0   0   0   0     0   0   0   1   0     0   1   1   1   0   0
C  0   0   0   0   0     0   0   0   0   0     0   1   1   1   0   0  
C  0   0   0   0   0     0   0   0   0   0     0   1   1   0   1   1  
C  0   0   0   0   0     0   0   0   0   0     0   1   1   0   1   1  
C  0   0   0   0   0     0   0   0   0   0     0   1   1   0   1   1  
C  0   0   0   0   0     0   0   0   0   0     0   1   1   0   1   1  
C  0   0   0   0   0     0   0   0   0   0     0   1   1   0   1   1  
C  0   0   0   0   0     0   0   0   0   0     0   1   1   0   1   1  
C  0   0   0   0   0     0   0   0   0   0     0   1   1   0   1   1  
C  0   0   0   0   0     0   0   0   0   0     0   1   1   0   1   1  
C  0   0   0   0   0     0   0   0   0   0     0   1   1   0   1   1  
C  0   0   0   0   0     0   0   0   0   0     0   1   1   0   0   0 
C  0   0   0   0   1     0   0   0   0   0     0   1   1   0   0   1
0  0   0   0   0   0     0   0   0   0   1     0   1   1   0   0   1
1  0   0   0   0   0     0   0   0   0   1     1   0   0   1   0   0
C  0   0   0   0   0     0   0   0   0   0     1   0   0   1   0   0  
C  0   0   0   0   0     0   0   0   0   0     1   0   0   0   1   1  
C  0   0   0   0   0     0   0   0   0   0     1   0   0   0   1   1  
C  0   0   0   0   0     0   0   0   0   0     1   0   0   0   1   1  
C  0   0   0   0   0     0   0   0   0   0     1   0   0   0   1   1  
C  0   0   0   0   0     0   0   0   0   0     1   0   0   0   1   1  
C  0   0   0   0   0     0   0   0   0   0     1   0   0   0   1   1  
C  0   0   0   0   0     0   0   0   0   0     1   0   0   0   1   1  
C  0   0   0   0   0     0   0   0   0   0     1   0   0   0   1   1  
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*/

/* Test case VIP:
CK P_0 P_1 P_2 P_3 P_VIP A_0 A_1 A_2 A_3 A_VIP y_2 y_1 y_0 z_2 z_1 z_0
0  0   1   1   1   1     0   0   0   0   0     0   0   0   0   0   0
C  0   0   0   0   0     0   0   0   0   0     0   0   0   0   0   1
0  0   0   0   0   0     0   1   0   0   0     0   0   0   0   0   1
1  0   0   0   0   0     0   1   0   0   0     0   0   1   0   0   1
C  0   0   0   0   0     0   0   0   0   0     0   0   1   0   0   1
0  0   0   0   0   0     0   0   1   0   0     0   0   1   0   0   1
1  0   0   0   0   0     0   0   1   0   0     0   1   0   0   0   1
C  0   0   0   0   0     0   0   0   0   0     0   1   0   0   0   1
0  0   0   0   0   0     0   0   0   1   0     0   1   0   0   0   1
1  0   0   0   0   0     0   0   0   1   0     0   1   1   0   0   1
C  0   0   0   0   0     0   0   0   0   0     0   1   1   0   0   1
0  0   0   0   0   0     0   0   0   0   1     0   1   1   0   0   1
1  0   0   0   0   0     0   0   0   0   1     1   0   0   1   0   0
C  0   0   0   0   0     0   0   0   0   0     1   0   0   1   0   0
C  0   0   0   0   0     0   0   0   0   0     1   0   0   0   1   1  
C  0   0   0   0   0     0   0   0   0   0     1   0   0   0   1   1  
C  0   0   0   0   0     0   0   0   0   0     1   0   0   0   1   1  
C  0   0   0   0   0     0   0   0   0   0     1   0   0   0   1   1  
C  0   0   0   0   0     0   0   0   0   0     1   0   0   0   1   1  
C  0   0   0   0   0     0   0   0   0   0     1   0   0   0   1   1  
C  0   0   0   0   0     0   0   0   0   0     1   0   0   0   1   1  
C  0   0   0   0   0     0   0   0   0   0     1   0   0   0   1   1  
C  0   0   0   0   0     0   0   0   0   0     1   0   0   0   1   1  
C  0   0   0   0   0     0   0   0   0   0     1   0   0   0   1   0  
0  0   0   0   0   0     0   0   0   1   0     1   0   0   0   1   0
1  0   0   0   0   0     0   0   0   1   0     0   1   1   1   0   0
C  0   0   0   0   0     0   0   0   0   0     0   1   1   1   0   0  
C  0   0   0   0   0     0   0   0   0   0     0   1   1   0   1   1  
C  0   0   0   0   0     0   0   0   0   0     0   1   1   0   1   1  
C  0   0   0   0   0     0   0   0   0   0     0   1   1   0   1   1  
C  0   0   0   0   1     0   0   0   0   0     0   1   1   0   1   1  
C  0   0   0   0   0     0   0   0   0   0     0   1   1   0   1   1  
C  0   0   0   0   0     0   0   0   0   0     0   1   1   0   1   1  
C  0   0   0   0   0     0   0   0   0   0     0   1   1   0   1   1  
C  0   0   0   0   0     0   0   0   0   0     0   1   1   0   1   1  
C  0   0   0   0   0     0   0   0   0   0     0   1   1   0   1   1  
C  0   0   0   0   0     0   0   0   0   0     0   1   1   0   0   1  
0  0   0   0   0   0     0   0   0   0   1     0   1   1   0   0   1
1  0   0   0   0   0     0   0   0   0   1     1   0   0   1   0   0
C  0   0   0   0   0     0   0   0   0   0     1   0   0   1   0   0
C  0   0   0   0   0     0   0   0   0   0     1   0   0   0   1   1  
C  0   0   0   0   0     0   0   0   0   0     1   0   0   0   1   1  
C  0   0   0   0   0     0   0   0   0   0     1   0   0   0   1   1  
C  0   0   0   0   0     0   0   0   0   0     1   0   0   0   1   1  
C  0   0   0   0   0     0   0   0   0   0     1   0   0   0   1   1  
C  0   0   0   0   0     0   0   0   0   0     1   0   0   0   1   1  
C  0   0   0   0   0     0   0   0   0   0     1   0   0   0   1   1  
C  0   0   0   0   0     0   0   0   0   0     1   0   0   0   1   1  
C  0   0   0   0   0     0   0   0   0   0     1   0   0   0   1   1  
C  0   0   0   0   0     0   0   0   0   0     1   0   0   0   1   0  
*/
