// Digital circuit circuit.dig as structural Verilog
module circuit (
  input  p_1,
  input  p_2,
  input  d_1,
  input  p_4,
  input  d_2,
  input  d_3,
  input  d_4,
  input  p_8,
  input  d_5,
  input  d_6,
  input  d_7,
  input  d_8,
  input  d,
  output y_1,
  output y_2,
  output y_3,
  output y_4,
  output y_5,
  output y_6,
  output y_7,
  output y_8,
  output y_9,
  output y_10,
  output y_11,
  output y_12,
  output e
);

  wire decoder_1_out_0, decoder_1_out_3, decoder_1_out_5, decoder_1_out_6, decoder_1_out_7, decoder_1_out_9,
       decoder_1_out_10, decoder_1_out_11, decoder_1_out_12;
  wire [3:0] xor_4_out, xor_5_out;
  wire [8:0] not_1_out;

  xor xor_1 (xor_4_out[0], d_1, d_2, d_4, d_5, d_7);
  xor xor_2 (xor_4_out[1], d_1, d_3, d_4, d_6, d_7);
  xor xor_3 (xor_4_out[2], d_2, d_3, d_4, d_8);
  xor xor_4 (xor_4_out[3], d_5, d_6, d_7, d_8);
  assign xor_5_out = {p_8, p_4, p_2, p_1} ^ xor_4_out;  // XOr xor_5, 4 bits wide
  Decoder #(.Selector_Bits(4)) decoder_1 (
    .sel(xor_5_out), .out_0(decoder_1_out_0), .out_3(decoder_1_out_3), .out_5(decoder_1_out_5),
    .out_6(decoder_1_out_6), .out_7(decoder_1_out_7), .out_9(decoder_1_out_9), .out_10(decoder_1_out_10),
    .out_11(decoder_1_out_11), .out_12(decoder_1_out_12));  // open: out_1, out_2, out_4, out_8, out_13, out_14, out_15
  not not_1 (not_1_out[0], decoder_1_out_0);
  xor xor_6 (not_1_out[1], decoder_1_out_3, d_1);
  xor xor_7 (not_1_out[2], decoder_1_out_5, d_2);
  xor xor_8 (not_1_out[3], decoder_1_out_6, d_3);
  xor xor_9 (not_1_out[4], decoder_1_out_7, d_4);
  xor xor_10 (not_1_out[5], decoder_1_out_9, d_5);
  xor xor_11 (not_1_out[6], decoder_1_out_10, d_6);
  xor xor_12 (not_1_out[7], decoder_1_out_11, d_7);
  xor xor_13 (not_1_out[8], decoder_1_out_12, d_8);
  Multiplexer #(.Bits(13)) multiplexer_1 (
    .sel(d),
    .in_0({d_8, d_7, d_6, d_5, xor_4_out[3], d_4, d_3, d_2, xor_4_out[2], d_1, xor_4_out[1:0], 1'b0}),
    .in_1({4'b0000, not_1_out}), .out({y_12, y_11, y_10, y_9, y_8, y_7, y_6, y_5, y_4, y_3, y_2, y_1, e}));

  // Notes on the sheet:
  //   Parity bit for decoding
  //   Parity bit for encoding
  //   Detecting and correcting an error
endmodule

/* Test case correzione:
d p_1 p_2 d_1 p_4 d_2 d_3 d_4 p_8 d_5 d_6 d_7 d_8 y_1 y_2 y_3 y_4 y_5 y_6 y_7 y_8 y_9 y_10 y_11 y_12 e
1 1 0 0 0 0 0 0 0 0 0 0 0 0 0 0 0 0 0 0 0 0 0 0 0 1
1 0 1 0 0 0 0 0 0 0 0 0 0 0 0 0 0 0 0 0 0 0 0 0 0 1
1 0 0 1 0 0 0 0 0 0 0 0 0 0 0 0 0 0 0 0 0 0 0 0 0 1
1 0 0 0 1 0 0 0 0 0 0 0 0 0 0 0 0 0 0 0 0 0 0 0 0 1
1 0 0 0 0 1 0 0 0 0 0 0 0 0 0 0 0 0 0 0 0 0 0 0 0 1
1 0 0 0 0 0 1 0 0 0 0 0 0 0 0 0 0 0 0 0 0 0 0 0 0 1
1 0 0 0 0 0 0 1 0 0 0 0 0 0 0 0 0 0 0 0 0 0 0 0 0 1
1 0 0 0 0 0 0 0 1 0 0 0 0 0 0 0 0 0 0 0 0 0 0 0 0 1
1 0 0 0 0 0 0 0 0 1 0 0 0 0 0 0 0 0 0 0 0 0 0 0 0 1
1 0 0 0 0 0 0 0 0 0 1 0 0 0 0 0 0 0 0 0 0 0 0 0 0 1
1 0 0 0 0 0 0 0 0 0 0 1 0 0 0 0 0 0 0 0 0 0 0 0 0 1
1 0 0 0 0 0 0 0 0 0 0 0 1 0 0 0 0 0 0 0 0 0 0 0 0 1
1 1 0 0 1 0 0 0 1 0 0 0 1 0 0 0 0 0 0 0 1 0 0 0 0 1
1 0 1 0 1 0 0 0 1 0 0 0 1 0 0 0 0 0 0 0 1 0 0 0 0 1
1 0 0 1 1 0 0 0 1 0 0 0 1 0 0 0 0 0 0 0 1 0 0 0 0 1
1 0 0 0 0 0 0 0 1 0 0 0 1 0 0 0 0 0 0 0 1 0 0 0 0 1
1 0 0 0 1 1 0 0 1 0 0 0 1 0 0 0 0 0 0 0 1 0 0 0 0 1
1 0 0 0 1 0 1 0 1 0 0 0 1 0 0 0 0 0 0 0 1 0 0 0 0 1
1 0 0 0 1 0 0 1 1 0 0 0 1 0 0 0 0 0 0 0 1 0 0 0 0 1
1 0 0 0 1 0 0 0 0 0 0 0 1 0 0 0 0 0 0 0 1 0 0 0 0 1
1 0 0 0 1 0 0 0 1 1 0 0 1 0 0 0 0 0 0 0 1 0 0 0 0 1
1 0 0 0 1 0 0 0 1 0 1 0 1 0 0 0 0 0 0 0 1 0 0 0 0 1
1 0 0 0 1 0 0 0 1 0 0 1 1 0 0 0 0 0 0 0 1 0 0 0 0 1
1 0 0 0 1 0 0 0 1 0 0 0 0 0 0 0 0 0 0 0 1 0 0 0 0 1
1 0 1 0 0 0 0 0 1 0 0 1 0 0 0 0 0 0 0 1 0 0 0 0 0 1
1 1 0 0 0 0 0 0 1 0 0 1 0 0 0 0 0 0 0 1 0 0 0 0 0 1
1 1 1 1 0 0 0 0 1 0 0 1 0 0 0 0 0 0 0 1 0 0 0 0 0 1
1 1 1 0 1 0 0 0 1 0 0 1 0 0 0 0 0 0 0 1 0 0 0 0 0 1
1 1 1 0 0 1 0 0 1 0 0 1 0 0 0 0 0 0 0 1 0 0 0 0 0 1
1 1 1 0 0 0 1 0 1 0 0 1 0 0 0 0 0 0 0 1 0 0 0 0 0 1
1 1 1 0 0 0 0 1 1 0 0 1 0 0 0 0 0 0 0 1 0 0 0 0 0 1
1 1 1 0 0 0 0 0 0 0 0 1 0 0 0 0 0 0 0 1 0 0 0 0 0 1
1 1 1 0 0 0 0 0 1 1 0 1 0 0 0 0 0 0 0 1 0 0 0 0 0 1
1 1 1 0 0 0 0 0 1 0 1 1 0 0 0 0 0 0 0 1 0 0 0 0 0 1
1 1 1 0 0 0 0 0 1 0 0 0 0 0 0 0 0 0 0 1 0 0 0 0 0 1
1 1 1 0 0 0 0 0 1 0 0 1 1 0 0 0 0 0 0 1 0 0 0 0 0 1
1 0 1 0 1 0 0 0 0 0 0 1 1 0 0 0 0 0 0 1 1 0 0 0 0 1
1 1 0 0 1 0 0 0 0 0 0 1 1 0 0 0 0 0 0 1 1 0 0 0 0 1
1 1 1 1 1 0 0 0 0 0 0 1 1 0 0 0 0 0 0 1 1 0 0 0 0 1
1 1 1 0 0 0 0 0 0 0 0 1 1 0 0 0 0 0 0 1 1 0 0 0 0 1
1 1 1 0 1 1 0 0 0 0 0 1 1 0 0 0 0 0 0 1 1 0 0 0 0 1
1 1 1 0 1 0 1 0 0 0 0 1 1 0 0 0 0 0 0 1 1 0 0 0 0 1
1 1 1 0 1 0 0 1 0 0 0 1 1 0 0 0 0 0 0 1 1 0 0 0 0 1
1 1 1 0 1 0 0 0 1 0 0 1 1 0 0 0 0 0 0 1 1 0 0 0 0 1
1 1 1 0 1 0 0 0 0 1 0 1 1 0 0 0 0 0 0 1 1 0 0 0 0 1
1 1 1 0 1 0 0 0 0 0 1 1 1 0 0 0 0 0 0 1 1 0 0 0 0 1
1 1 1 0 1 0 0 0 0 0 0 0 1 0 0 0 0 0 0 1 1 0 0 0 0 1
1 1 1 0 1 0 0 0 0 0 0 1 0 0 0 0 0 0 0 1 1 0 0 0 0 1
1 1 1 0 0 0 0 0 1 0 1 0 0 0 0 0 0 0 1 0 0 0 0 0 0 1
1 0 0 0 0 0 0 0 1 0 1 0 0 0 0 0 0 0 1 0 0 0 0 0 0 1
1 0 1 1 0 0 0 0 1 0 1 0 0 0 0 0 0 0 1 0 0 0 0 0 0 1
1 0 1 0 1 0 0 0 1 0 1 0 0 0 0 0 0 0 1 0 0 0 0 0 0 1
1 0 1 0 0 1 0 0 1 0 1 0 0 0 0 0 0 0 1 0 0 0 0 0 0 1
1 0 1 0 0 0 1 0 1 0 1 0 0 0 0 0 0 0 1 0 0 0 0 0 0 1
1 0 1 0 0 0 0 1 1 0 1 0 0 0 0 0 0 0 1 0 0 0 0 0 0 1
1 0 1 0 0 0 0 0 0 0 1 0 0 0 0 0 0 0 1 0 0 0 0 0 0 1
1 0 1 0 0 0 0 0 1 1 1 0 0 0 0 0 0 0 1 0 0 0 0 0 0 1
1 0 1 0 0 0 0 0 1 0 0 0 0 0 0 0 0 0 1 0 0 0 0 0 0 1
1 0 1 0 0 0 0 0 1 0 1 1 0 0 0 0 0 0 1 0 0 0 0 0 0 1
1 0 1 0 0 0 0 0 1 0 1 0 1 0 0 0 0 0 1 0 0 0 0 0 0 1
1 1 1 0 1 0 0 0 0 0 1 0 1 0 0 0 0 0 1 0 1 0 0 0 0 1
1 0 0 0 1 0 0 0 0 0 1 0 1 0 0 0 0 0 1 0 1 0 0 0 0 1
1 0 1 1 1 0 0 0 0 0 1 0 1 0 0 0 0 0 1 0 1 0 0 0 0 1
1 0 1 0 0 0 0 0 0 0 1 0 1 0 0 0 0 0 1 0 1 0 0 0 0 1
1 0 1 0 1 1 0 0 0 0 1 0 1 0 0 0 0 0 1 0 1 0 0 0 0 1
1 0 1 0 1 0 1 0 0 0 1 0 1 0 0 0 0 0 1 0 1 0 0 0 0 1
1 0 1 0 1 0 0 1 0 0 1 0 1 0 0 0 0 0 1 0 1 0 0 0 0 1
1 0 1 0 1 0 0 0 1 0 1 0 1 0 0 0 0 0 1 0 1 0 0 0 0 1
1 0 1 0 1 0 0 0 0 1 1 0 1 0 0 0 0 0 1 0 1 0 0 0 0 1
1 0 1 0 1 0 0 0 0 0 0 0 1 0 0 0 0 0 1 0 1 0 0 0 0 1
1 0 1 0 1 0 0 0 0 0 1 1 1 0 0 0 0 0 1 0 1 0 0 0 0 1
1 0 1 0 1 0 0 0 0 0 1 0 0 0 0 0 0 0 1 0 1 0 0 0 0 1
1 0 0 0 0 0 0 0 0 0 1 1 0 0 0 0 0 0 1 1 0 0 0 0 0 1
1 1 1 0 0 0 0 0 0 0 1 1 0 0 0 0 0 0 1 1 0 0 0 0 0 1
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*/

/* Test case codifica:
d p_1 p_2 d_1 p_4 d_2 d_3 d_4 p_8 d_5 d_6 d_7 d_8 y_1 y_2 y_3 y_4 y_5 y_6 y_7 y_8 y_9 y_10 y_11 y_12 e
0 X X 0 X 0 0 0 X 0 0 0 0 0 0 0 0 0 0 0 0 0 0 0 0 0
0 X X 0 X 0 0 0 X 0 0 0 1 0 0 0 1 0 0 0 1 0 0 0 1 0
0 X X 0 X 0 0 0 X 0 0 1 0 1 1 0 0 0 0 0 1 0 0 1 0 0
0 X X 0 X 0 0 0 X 0 0 1 1 1 1 0 1 0 0 0 0 0 0 1 1 0
0 X X 0 X 0 0 0 X 0 1 0 0 0 1 0 0 0 0 0 1 0 1 0 0 0
0 X X 0 X 0 0 0 X 0 1 0 1 0 1 0 1 0 0 0 0 0 1 0 1 0
0 X X 0 X 0 0 0 X 0 1 1 0 1 0 0 0 0 0 0 0 0 1 1 0 0
0 X X 0 X 0 0 0 X 0 1 1 1 1 0 0 1 0 0 0 1 0 1 1 1 0
0 X X 0 X 0 0 0 X 1 0 0 0 1 0 0 0 0 0 0 1 1 0 0 0 0
0 X X 0 X 0 0 0 X 1 0 0 1 1 0 0 1 0 0 0 0 1 0 0 1 0
0 X X 0 X 0 0 0 X 1 0 1 0 0 1 0 0 0 0 0 0 1 0 1 0 0
0 X X 0 X 0 0 0 X 1 0 1 1 0 1 0 1 0 0 0 1 1 0 1 1 0
0 X X 0 X 0 0 0 X 1 1 0 0 1 1 0 0 0 0 0 0 1 1 0 0 0
0 X X 0 X 0 0 0 X 1 1 0 1 1 1 0 1 0 0 0 1 1 1 0 1 0
0 X X 0 X 0 0 0 X 1 1 1 0 0 0 0 0 0 0 0 1 1 1 1 0 0
0 X X 0 X 0 0 0 X 1 1 1 1 0 0 0 1 0 0 0 0 1 1 1 1 0
0 X X 0 X 0 0 1 X 0 0 0 0 1 1 0 1 0 0 1 0 0 0 0 0 0
0 X X 0 X 0 0 1 X 0 0 0 1 1 1 0 0 0 0 1 1 0 0 0 1 0
0 X X 0 X 0 0 1 X 0 0 1 0 0 0 0 1 0 0 1 1 0 0 1 0 0
0 X X 0 X 0 0 1 X 0 0 1 1 0 0 0 0 0 0 1 0 0 0 1 1 0
0 X X 0 X 0 0 1 X 0 1 0 0 1 0 0 1 0 0 1 1 0 1 0 0 0
0 X X 0 X 0 0 1 X 0 1 0 1 1 0 0 0 0 0 1 0 0 1 0 1 0
0 X X 0 X 0 0 1 X 0 1 1 0 0 1 0 1 0 0 1 0 0 1 1 0 0
0 X X 0 X 0 0 1 X 0 1 1 1 0 1 0 0 0 0 1 1 0 1 1 1 0
0 X X 0 X 0 0 1 X 1 0 0 0 0 1 0 1 0 0 1 1 1 0 0 0 0
0 X X 0 X 0 0 1 X 1 0 0 1 0 1 0 0 0 0 1 0 1 0 0 1 0
0 X X 0 X 0 0 1 X 1 0 1 0 1 0 0 1 0 0 1 0 1 0 1 0 0
0 X X 0 X 0 0 1 X 1 0 1 1 1 0 0 0 0 0 1 1 1 0 1 1 0
0 X X 0 X 0 0 1 X 1 1 0 0 0 0 0 1 0 0 1 0 1 1 0 0 0
0 X X 0 X 0 0 1 X 1 1 0 1 0 0 0 0 0 0 1 1 1 1 0 1 0
0 X X 0 X 0 0 1 X 1 1 1 0 1 1 0 1 0 0 1 1 1 1 1 0 0
0 X X 0 X 0 0 1 X 1 1 1 1 1 1 0 0 0 0 1 0 1 1 1 1 0
0 X X 0 X 0 1 0 X 0 0 0 0 0 1 0 1 0 1 0 0 0 0 0 0 0
0 X X 0 X 0 1 0 X 0 0 0 1 0 1 0 0 0 1 0 1 0 0 0 1 0
0 X X 0 X 0 1 0 X 0 0 1 0 1 0 0 1 0 1 0 1 0 0 1 0 0
0 X X 0 X 0 1 0 X 0 0 1 1 1 0 0 0 0 1 0 0 0 0 1 1 0
0 X X 0 X 0 1 0 X 0 1 0 0 0 0 0 1 0 1 0 1 0 1 0 0 0
0 X X 0 X 0 1 0 X 0 1 0 1 0 0 0 0 0 1 0 0 0 1 0 1 0
0 X X 0 X 0 1 0 X 0 1 1 0 1 1 0 1 0 1 0 0 0 1 1 0 0
0 X X 0 X 0 1 0 X 0 1 1 1 1 1 0 0 0 1 0 1 0 1 1 1 0
0 X X 0 X 0 1 0 X 1 0 0 0 1 1 0 1 0 1 0 1 1 0 0 0 0
0 X X 0 X 0 1 0 X 1 0 0 1 1 1 0 0 0 1 0 0 1 0 0 1 0
0 X X 0 X 0 1 0 X 1 0 1 0 0 0 0 1 0 1 0 0 1 0 1 0 0
0 X X 0 X 0 1 0 X 1 0 1 1 0 0 0 0 0 1 0 1 1 0 1 1 0
0 X X 0 X 0 1 0 X 1 1 0 0 1 0 0 1 0 1 0 0 1 1 0 0 0
0 X X 0 X 0 1 0 X 1 1 0 1 1 0 0 0 0 1 0 1 1 1 0 1 0
0 X X 0 X 0 1 0 X 1 1 1 0 0 1 0 1 0 1 0 1 1 1 1 0 0
0 X X 0 X 0 1 0 X 1 1 1 1 0 1 0 0 0 1 0 0 1 1 1 1 0
0 X X 0 X 0 1 1 X 0 0 0 0 1 0 0 0 0 1 1 0 0 0 0 0 0
0 X X 0 X 0 1 1 X 0 0 0 1 1 0 0 1 0 1 1 1 0 0 0 1 0
0 X X 0 X 0 1 1 X 0 0 1 0 0 1 0 0 0 1 1 1 0 0 1 0 0
0 X X 0 X 0 1 1 X 0 0 1 1 0 1 0 1 0 1 1 0 0 0 1 1 0
0 X X 0 X 0 1 1 X 0 1 0 0 1 1 0 0 0 1 1 1 0 1 0 0 0
0 X X 0 X 0 1 1 X 0 1 0 1 1 1 0 1 0 1 1 0 0 1 0 1 0
0 X X 0 X 0 1 1 X 0 1 1 0 0 0 0 0 0 1 1 0 0 1 1 0 0
0 X X 0 X 0 1 1 X 0 1 1 1 0 0 0 1 0 1 1 1 0 1 1 1 0
0 X X 0 X 0 1 1 X 1 0 0 0 0 0 0 0 0 1 1 1 1 0 0 0 0
0 X X 0 X 0 1 1 X 1 0 0 1 0 0 0 1 0 1 1 0 1 0 0 1 0
0 X X 0 X 0 1 1 X 1 0 1 0 1 1 0 0 0 1 1 0 1 0 1 0 0
0 X X 0 X 0 1 1 X 1 0 1 1 1 1 0 1 0 1 1 1 1 0 1 1 0
0 X X 0 X 0 1 1 X 1 1 0 0 0 1 0 0 0 1 1 0 1 1 0 0 0
0 X X 0 X 0 1 1 X 1 1 0 1 0 1 0 1 0 1 1 1 1 1 0 1 0
0 X X 0 X 0 1 1 X 1 1 1 0 1 0 0 0 0 1 1 1 1 1 1 0 0
0 X X 0 X 0 1 1 X 1 1 1 1 1 0 0 1 0 1 1 0 1 1 1 1 0
0 X X 0 X 1 0 0 X 0 0 0 0 1 0 0 1 1 0 0 0 0 0 0 0 0
0 X X 0 X 1 0 0 X 0 0 0 1 1 0 0 0 1 0 0 1 0 0 0 1 0
0 X X 0 X 1 0 0 X 0 0 1 0 0 1 0 1 1 0 0 1 0 0 1 0 0
0 X X 0 X 1 0 0 X 0 0 1 1 0 1 0 0 1 0 0 0 0 0 1 1 0
0 X X 0 X 1 0 0 X 0 1 0 0 1 1 0 1 1 0 0 1 0 1 0 0 0
0 X X 0 X 1 0 0 X 0 1 0 1 1 1 0 0 1 0 0 0 0 1 0 1 0
0 X X 0 X 1 0 0 X 0 1 1 0 0 0 0 1 1 0 0 0 0 1 1 0 0
0 X X 0 X 1 0 0 X 0 1 1 1 0 0 0 0 1 0 0 1 0 1 1 1 0
0 X X 0 X 1 0 0 X 1 0 0 0 0 0 0 1 1 0 0 1 1 0 0 0 0
0 X X 0 X 1 0 0 X 1 0 0 1 0 0 0 0 1 0 0 0 1 0 0 1 0
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*/

/* Test case decodifica:
d p_1 p_2 d_1 p_4 d_2 d_3 d_4 p_8 d_5 d_6 d_7 d_8 y_1 y_2 y_3 y_4 y_5 y_6 y_7 y_8 y_9 y_10 y_11 y_12 e
1 0 0 0 0 0 0 0 0 0 0 0 0 0 0 0 0 0 0 0 0 0 0 0 0 0
1 0 0 0 1 0 0 0 1 0 0 0 1 0 0 0 0 0 0 0 1 0 0 0 0 0
1 1 1 0 0 0 0 0 1 0 0 1 0 0 0 0 0 0 0 1 0 0 0 0 0 0
1 1 1 0 1 0 0 0 0 0 0 1 1 0 0 0 0 0 0 1 1 0 0 0 0 0
1 0 1 0 0 0 0 0 1 0 1 0 0 0 0 0 0 0 1 0 0 0 0 0 0 0
1 0 1 0 1 0 0 0 0 0 1 0 1 0 0 0 0 0 1 0 1 0 0 0 0 0
1 1 0 0 0 0 0 0 0 0 1 1 0 0 0 0 0 0 1 1 0 0 0 0 0 0
1 1 0 0 1 0 0 0 1 0 1 1 1 0 0 0 0 0 1 1 1 0 0 0 0 0
1 1 0 0 0 0 0 0 1 1 0 0 0 0 0 0 0 1 0 0 0 0 0 0 0 0
1 1 0 0 1 0 0 0 0 1 0 0 1 0 0 0 0 1 0 0 1 0 0 0 0 0
1 0 1 0 0 0 0 0 0 1 0 1 0 0 0 0 0 1 0 1 0 0 0 0 0 0
1 0 1 0 1 0 0 0 1 1 0 1 1 0 0 0 0 1 0 1 1 0 0 0 0 0
1 1 1 0 0 0 0 0 0 1 1 0 0 0 0 0 0 1 1 0 0 0 0 0 0 0
1 1 1 0 1 0 0 0 1 1 1 0 1 0 0 0 0 1 1 0 1 0 0 0 0 0
1 0 0 0 0 0 0 0 1 1 1 1 0 0 0 0 0 1 1 1 0 0 0 0 0 0
1 0 0 0 1 0 0 0 0 1 1 1 1 0 0 0 0 1 1 1 1 0 0 0 0 0
1 1 1 0 1 0 0 1 0 0 0 0 0 0 0 0 1 0 0 0 0 0 0 0 0 0
1 1 1 0 0 0 0 1 1 0 0 0 1 0 0 0 1 0 0 0 1 0 0 0 0 0
1 0 0 0 1 0 0 1 1 0 0 1 0 0 0 0 1 0 0 1 0 0 0 0 0 0
1 0 0 0 0 0 0 1 0 0 0 1 1 0 0 0 1 0 0 1 1 0 0 0 0 0
1 1 0 0 1 0 0 1 1 0 1 0 0 0 0 0 1 0 1 0 0 0 0 0 0 0
1 1 0 0 0 0 0 1 0 0 1 0 1 0 0 0 1 0 1 0 1 0 0 0 0 0
1 0 1 0 1 0 0 1 0 0 1 1 0 0 0 0 1 0 1 1 0 0 0 0 0 0
1 0 1 0 0 0 0 1 1 0 1 1 1 0 0 0 1 0 1 1 1 0 0 0 0 0
1 0 1 0 1 0 0 1 1 1 0 0 0 0 0 0 1 1 0 0 0 0 0 0 0 0
1 0 1 0 0 0 0 1 0 1 0 0 1 0 0 0 1 1 0 0 1 0 0 0 0 0
1 1 0 0 1 0 0 1 0 1 0 1 0 0 0 0 1 1 0 1 0 0 0 0 0 0
1 1 0 0 0 0 0 1 1 1 0 1 1 0 0 0 1 1 0 1 1 0 0 0 0 0
1 0 0 0 1 0 0 1 0 1 1 0 0 0 0 0 1 1 1 0 0 0 0 0 0 0
1 0 0 0 0 0 0 1 1 1 1 0 1 0 0 0 1 1 1 0 1 0 0 0 0 0
1 1 1 0 1 0 0 1 1 1 1 1 0 0 0 0 1 1 1 1 0 0 0 0 0 0
1 1 1 0 0 0 0 1 0 1 1 1 1 0 0 0 1 1 1 1 1 0 0 0 0 0
1 0 1 0 1 0 1 0 0 0 0 0 0 0 0 1 0 0 0 0 0 0 0 0 0 0
1 0 1 0 0 0 1 0 1 0 0 0 1 0 0 1 0 0 0 0 1 0 0 0 0 0
1 1 0 0 1 0 1 0 1 0 0 1 0 0 0 1 0 0 0 1 0 0 0 0 0 0
1 1 0 0 0 0 1 0 0 0 0 1 1 0 0 1 0 0 0 1 1 0 0 0 0 0
1 0 0 0 1 0 1 0 1 0 1 0 0 0 0 1 0 0 1 0 0 0 0 0 0 0
1 0 0 0 0 0 1 0 0 0 1 0 1 0 0 1 0 0 1 0 1 0 0 0 0 0
1 1 1 0 1 0 1 0 0 0 1 1 0 0 0 1 0 0 1 1 0 0 0 0 0 0
1 1 1 0 0 0 1 0 1 0 1 1 1 0 0 1 0 0 1 1 1 0 0 0 0 0
1 1 1 0 1 0 1 0 1 1 0 0 0 0 0 1 0 1 0 0 0 0 0 0 0 0
1 1 1 0 0 0 1 0 0 1 0 0 1 0 0 1 0 1 0 0 1 0 0 0 0 0
1 0 0 0 1 0 1 0 0 1 0 1 0 0 0 1 0 1 0 1 0 0 0 0 0 0
1 0 0 0 0 0 1 0 1 1 0 1 1 0 0 1 0 1 0 1 1 0 0 0 0 0
1 1 0 0 1 0 1 0 0 1 1 0 0 0 0 1 0 1 1 0 0 0 0 0 0 0
1 1 0 0 0 0 1 0 1 1 1 0 1 0 0 1 0 1 1 0 1 0 0 0 0 0
1 0 1 0 1 0 1 0 1 1 1 1 0 0 0 1 0 1 1 1 0 0 0 0 0 0
1 0 1 0 0 0 1 0 0 1 1 1 1 0 0 1 0 1 1 1 1 0 0 0 0 0
1 1 0 0 0 0 1 1 0 0 0 0 0 0 0 1 1 0 0 0 0 0 0 0 0 0
1 1 0 0 1 0 1 1 1 0 0 0 1 0 0 1 1 0 0 0 1 0 0 0 0 0
1 0 1 0 0 0 1 1 1 0 0 1 0 0 0 1 1 0 0 1 0 0 0 0 0 0
1 0 1 0 1 0 1 1 0 0 0 1 1 0 0 1 1 0 0 1 1 0 0 0 0 0
1 1 1 0 0 0 1 1 1 0 1 0 0 0 0 1 1 0 1 0 0 0 0 0 0 0
1 1 1 0 1 0 1 1 0 0 1 0 1 0 0 1 1 0 1 0 1 0 0 0 0 0
1 0 0 0 0 0 1 1 0 0 1 1 0 0 0 1 1 0 1 1 0 0 0 0 0 0
1 0 0 0 1 0 1 1 1 0 1 1 1 0 0 1 1 0 1 1 1 0 0 0 0 0
1 0 0 0 0 0 1 1 1 1 0 0 0 0 0 1 1 1 0 0 0 0 0 0 0 0
1 0 0 0 1 0 1 1 0 1 0 0 1 0 0 1 1 1 0 0 1 0 0 0 0 0
1 1 1 0 0 0 1 1 0 1 0 1 0 0 0 1 1 1 0 1 0 0 0 0 0 0
1 1 1 0 1 0 1 1 1 1 0 1 1 0 0 1 1 1 0 1 1 0 0 0 0 0
1 0 1 0 0 0 1 1 0 1 1 0 0 0 0 1 1 1 1 0 0 0 0 0 0 0
1 0 1 0 1 0 1 1 1 1 1 0 1 0 0 1 1 1 1 0 1 0 0 0 0 0
1 1 0 0 0 0 1 1 1 1 1 1 0 0 0 1 1 1 1 1 0 0 0 0 0 0
1 1 0 0 1 0 1 1 0 1 1 1 1 0 0 1 1 1 1 1 1 0 0 0 0 0
1 1 0 0 1 1 0 0 0 0 0 0 0 0 1 0 0 0 0 0 0 0 0 0 0 0
1 1 0 0 0 1 0 0 1 0 0 0 1 0 1 0 0 0 0 0 1 0 0 0 0 0
1 0 1 0 1 1 0 0 1 0 0 1 0 0 1 0 0 0 0 1 0 0 0 0 0 0
1 0 1 0 0 1 0 0 0 0 0 1 1 0 1 0 0 0 0 1 1 0 0 0 0 0
1 1 1 0 1 1 0 0 1 0 1 0 0 0 1 0 0 0 1 0 0 0 0 0 0 0
1 1 1 0 0 1 0 0 0 0 1 0 1 0 1 0 0 0 1 0 1 0 0 0 0 0
1 0 0 0 1 1 0 0 0 0 1 1 0 0 1 0 0 0 1 1 0 0 0 0 0 0
1 0 0 0 0 1 0 0 1 0 1 1 1 0 1 0 0 0 1 1 1 0 0 0 0 0
1 0 0 0 1 1 0 0 1 1 0 0 0 0 1 0 0 1 0 0 0 0 0 0 0 0
1 0 0 0 0 1 0 0 0 1 0 0 1 0 1 0 0 1 0 0 1 0 0 0 0 0
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*/

/* Test case detect:
d p_1 p_2 d_1 p_4 d_2 d_3 d_4 p_8 d_5 d_6 d_7 d_8 y_1 y_2 y_3 y_4 y_5 y_6 y_7 y_8 y_9 y_10 y_11 y_12 e
1 1 0 0 0 0 0 0 0 0 0 0 0 X X X X X X X X X X X X 1
1 1 1 0 0 0 0 0 0 0 0 0 0 X X X X X X X X X X X X 1
1 1 0 1 0 0 0 0 0 0 0 0 0 X X X X X X X X X X X X 1
1 1 0 0 1 0 0 0 0 0 0 0 0 X X X X X X X X X X X X 1
1 1 0 0 0 1 0 0 0 0 0 0 0 X X X X X X X X X X X X 1
1 1 0 0 0 0 1 0 0 0 0 0 0 X X X X X X X X X X X X 1
1 1 0 0 0 0 0 1 0 0 0 0 0 X X X X X X X X X X X X 1
1 1 0 0 0 0 0 0 1 0 0 0 0 X X X X X X X X X X X X 1
1 1 0 0 0 0 0 0 0 1 0 0 0 X X X X X X X X X X X X 1
1 1 0 0 0 0 0 0 0 0 1 0 0 X X X X X X X X X X X X 1
1 1 0 0 0 0 0 0 0 0 0 1 0 X X X X X X X X X X X X 1
1 1 0 0 0 0 0 0 0 0 0 0 1 X X X X X X X X X X X X 1
1 0 1 0 0 0 0 0 0 0 0 0 0 X X X X X X X X X X X X 1
1 1 1 0 0 0 0 0 0 0 0 0 0 X X X X X X X X X X X X 1
1 0 1 1 0 0 0 0 0 0 0 0 0 X X X X X X X X X X X X 1
1 0 1 0 1 0 0 0 0 0 0 0 0 X X X X X X X X X X X X 1
1 0 1 0 0 1 0 0 0 0 0 0 0 X X X X X X X X X X X X 1
1 0 1 0 0 0 1 0 0 0 0 0 0 X X X X X X X X X X X X 1
1 0 1 0 0 0 0 1 0 0 0 0 0 X X X X X X X X X X X X 1
1 0 1 0 0 0 0 0 1 0 0 0 0 X X X X X X X X X X X X 1
1 0 1 0 0 0 0 0 0 1 0 0 0 X X X X X X X X X X X X 1
1 0 1 0 0 0 0 0 0 0 1 0 0 X X X X X X X X X X X X 1
1 0 1 0 0 0 0 0 0 0 0 1 0 X X X X X X X X X X X X 1
1 0 1 0 0 0 0 0 0 0 0 0 1 X X X X X X X X X X X X 1
1 0 0 1 0 0 0 0 0 0 0 0 0 X X X X X X X X X X X X 1
1 1 0 1 0 0 0 0 0 0 0 0 0 X X X X X X X X X X X X 1
1 0 1 1 0 0 0 0 0 0 0 0 0 X X X X X X X X X X X X 1
1 0 0 1 1 0 0 0 0 0 0 0 0 X X X X X X X X X X X X 1
1 0 0 1 0 1 0 0 0 0 0 0 0 X X X X X X X X X X X X 1
1 0 0 1 0 0 1 0 0 0 0 0 0 X X X X X X X X X X X X 1
1 0 0 1 0 0 0 1 0 0 0 0 0 X X X X X X X X X X X X 1
1 0 0 1 0 0 0 0 1 0 0 0 0 X X X X X X X X X X X X 1
1 0 0 1 0 0 0 0 0 1 0 0 0 X X X X X X X X X X X X 1
1 0 0 1 0 0 0 0 0 0 1 0 0 X X X X X X X X X X X X 1
1 0 0 1 0 0 0 0 0 0 0 1 0 X X X X X X X X X X X X 1
1 0 0 1 0 0 0 0 0 0 0 0 1 X X X X X X X X X X X X 1
1 0 0 0 1 0 0 0 0 0 0 0 0 X X X X X X X X X X X X 1
1 1 0 0 1 0 0 0 0 0 0 0 0 X X X X X X X X X X X X 1
1 0 1 0 1 0 0 0 0 0 0 0 0 X X X X X X X X X X X X 1
1 0 0 1 1 0 0 0 0 0 0 0 0 X X X X X X X X X X X X 1
1 0 0 0 1 1 0 0 0 0 0 0 0 X X X X X X X X X X X X 1
1 0 0 0 1 0 1 0 0 0 0 0 0 X X X X X X X X X X X X 1
1 0 0 0 1 0 0 1 0 0 0 0 0 X X X X X X X X X X X X 1
1 0 0 0 1 0 0 0 1 0 0 0 0 X X X X X X X X X X X X 1
1 0 0 0 1 0 0 0 0 1 0 0 0 X X X X X X X X X X X X 1
1 0 0 0 1 0 0 0 0 0 1 0 0 X X X X X X X X X X X X 1
1 0 0 0 1 0 0 0 0 0 0 1 0 X X X X X X X X X X X X 1
1 0 0 0 1 0 0 0 0 0 0 0 1 X X X X X X X X X X X X 1
1 0 0 0 0 1 0 0 0 0 0 0 0 X X X X X X X X X X X X 1
1 1 0 0 0 1 0 0 0 0 0 0 0 X X X X X X X X X X X X 1
1 0 1 0 0 1 0 0 0 0 0 0 0 X X X X X X X X X X X X 1
1 0 0 1 0 1 0 0 0 0 0 0 0 X X X X X X X X X X X X 1
1 0 0 0 1 1 0 0 0 0 0 0 0 X X X X X X X X X X X X 1
1 0 0 0 0 1 1 0 0 0 0 0 0 X X X X X X X X X X X X 1
1 0 0 0 0 1 0 1 0 0 0 0 0 X X X X X X X X X X X X 1
1 0 0 0 0 1 0 0 1 0 0 0 0 X X X X X X X X X X X X 1
1 0 0 0 0 1 0 0 0 1 0 0 0 X X X X X X X X X X X X 1
1 0 0 0 0 1 0 0 0 0 1 0 0 X X X X X X X X X X X X 1
1 0 0 0 0 1 0 0 0 0 0 1 0 X X X X X X X X X X X X 1
1 0 0 0 0 1 0 0 0 0 0 0 1 X X X X X X X X X X X X 1
1 0 0 0 0 0 1 0 0 0 0 0 0 X X X X X X X X X X X X 1
1 1 0 0 0 0 1 0 0 0 0 0 0 X X X X X X X X X X X X 1
1 0 1 0 0 0 1 0 0 0 0 0 0 X X X X X X X X X X X X 1
1 0 0 1 0 0 1 0 0 0 0 0 0 X X X X X X X X X X X X 1
1 0 0 0 1 0 1 0 0 0 0 0 0 X X X X X X X X X X X X 1
1 0 0 0 0 1 1 0 0 0 0 0 0 X X X X X X X X X X X X 1
1 0 0 0 0 0 1 1 0 0 0 0 0 X X X X X X X X X X X X 1
1 0 0 0 0 0 1 0 1 0 0 0 0 X X X X X X X X X X X X 1
1 0 0 0 0 0 1 0 0 1 0 0 0 X X X X X X X X X X X X 1
1 0 0 0 0 0 1 0 0 0 1 0 0 X X X X X X X X X X X X 1
1 0 0 0 0 0 1 0 0 0 0 1 0 X X X X X X X X X X X X 1
1 0 0 0 0 0 1 0 0 0 0 0 1 X X X X X X X X X X X X 1
1 0 0 0 0 0 0 1 0 0 0 0 0 X X X X X X X X X X X X 1
1 1 0 0 0 0 0 1 0 0 0 0 0 X X X X X X X X X X X X 1
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*/
