// Digital circuit circuit.dig as structural Verilog
module circuit (
  input  A,
  input  B,
  input  C,
  input  D,
  output S,
  output Y1,
  output Y2,
  output Y3
);

  not not_1 (Y3, A);
  nand nand_1 (Y2, A, B);
  nand nand_2 (Y1, A, B, C);
  nand nand_3 (S, A, B, C, D);
endmodule
