// Digital circuit circuit.dig as structural Verilog
module circuit (
  input  x_1,
  input  x_0,
  input  CK,
  output z
);

  wire y_0, y_1, y_2;
  wire [2:0] ROM_d;

  ROM #(.AddrBits(5), .Bits(4)) ROM (.A({y_2, y_1, y_0, x_0, x_1}), .sel(1'b1), .D({z, ROM_d}));
  D_FF d_ff_1 (.D(ROM_d[0]), .C(CK), .Q(y_2));  // open: nQ
  D_FF d_ff_2 (.D(ROM_d[1]), .C(CK), .Q(y_1));  // open: nQ
  D_FF d_ff_3 (.D(ROM_d[2]), .C(CK), .Q(y_0));  // open: nQ

  // Notes on the sheet:
  //   Character Encoding
  //   Combinational Logic
  //   ROM loads mealy.hex
endmodule
